// Logisim project Lab_7_8.circ as structural Verilog
module Edge_D (
  input  Rd,
  input  D,
  input  Sd,
  input  CP,
  output Qn,
  output Q
);

  wire nand_1_out, nand_2_out, nand_3_out, nand_4_out;

  nand nand_1 (nand_1_out, nand_3_out, D);
  nand nand_2 (nand_2_out, nand_1_out, nand_4_out);
  nand nand_3 (nand_3_out, CP, nand_1_out, nand_4_out);
  nand nand_4 (nand_4_out, nand_2_out, CP);
  nand nand_5 (Qn, Rd, nand_3_out, Q);
  nand nand_6 (Q, Qn, nand_4_out, Sd);
endmodule

module Reg1 (
  input  Rd,
  input  Sd,
  input  DIn,
  input  in_4,
  input  WE,
  output QOut
);

  wire multiplexer_1_out;

  Multiplexer #(.select(1), .width(1), .disabled("Z"), .enable("false")) multiplexer_1 (
    .in0(QOut), .in1(DIn), .out(multiplexer_1_out), .sel(WE));
  Edge_D edge_d_1 (.Rd(Rd), .D(multiplexer_1_out), .Sd(Sd), .CP(in_4), .Q(QOut));  // open: Qn

  // Notes on the sheet:
  //   CLK
endmodule

module Reg32 (
  input  Sd,
  input  WE,
  input  Rd,
  input  CLK,
  input  [31:0] in_5,
  output [31:0] out_6
);

  Reg1 reg1_1 (.Rd(Rd), .DIn(in_5[0]), .in_4(CLK), .WE(WE), .Sd(Sd), .QOut(out_6[0]));
  Reg1 reg1_2 (.Rd(Rd), .DIn(in_5[1]), .in_4(CLK), .WE(WE), .Sd(Sd), .QOut(out_6[1]));
  Reg1 reg1_3 (.Rd(Rd), .DIn(in_5[2]), .in_4(CLK), .WE(WE), .Sd(Sd), .QOut(out_6[2]));
  Reg1 reg1_4 (.Rd(Rd), .DIn(in_5[3]), .in_4(CLK), .WE(WE), .Sd(Sd), .QOut(out_6[3]));
  Reg1 reg1_5 (.Rd(Rd), .DIn(in_5[4]), .in_4(CLK), .WE(WE), .Sd(Sd), .QOut(out_6[4]));
  Reg1 reg1_6 (.Rd(Rd), .DIn(in_5[5]), .in_4(CLK), .WE(WE), .Sd(Sd), .QOut(out_6[5]));
  Reg1 reg1_7 (.Rd(Rd), .DIn(in_5[6]), .in_4(CLK), .WE(WE), .Sd(Sd), .QOut(out_6[6]));
  Reg1 reg1_8 (.Rd(Rd), .DIn(in_5[7]), .in_4(CLK), .WE(WE), .Sd(Sd), .QOut(out_6[7]));
  Reg1 reg1_9 (.Rd(Rd), .DIn(in_5[8]), .in_4(CLK), .WE(WE), .Sd(Sd), .QOut(out_6[8]));
  Reg1 reg1_10 (.Rd(Rd), .DIn(in_5[9]), .in_4(CLK), .WE(WE), .Sd(Sd), .QOut(out_6[9]));
  Reg1 reg1_11 (.Rd(Rd), .DIn(in_5[10]), .in_4(CLK), .WE(WE), .Sd(Sd), .QOut(out_6[10]));
  Reg1 reg1_12 (.Rd(Rd), .DIn(in_5[11]), .in_4(CLK), .WE(WE), .Sd(Sd), .QOut(out_6[11]));
  Reg1 reg1_13 (.Rd(Rd), .DIn(in_5[12]), .in_4(CLK), .WE(WE), .Sd(Sd), .QOut(out_6[12]));
  Reg1 reg1_14 (.Rd(Rd), .DIn(in_5[13]), .in_4(CLK), .WE(WE), .Sd(Sd), .QOut(out_6[13]));
  Reg1 reg1_15 (.Rd(Rd), .DIn(in_5[14]), .in_4(CLK), .WE(WE), .Sd(Sd), .QOut(out_6[14]));
  Reg1 reg1_16 (.Rd(Rd), .DIn(in_5[15]), .in_4(CLK), .WE(WE), .Sd(Sd), .QOut(out_6[15]));
  Reg1 reg1_17 (.Rd(Rd), .DIn(in_5[16]), .in_4(CLK), .WE(WE), .Sd(Sd), .QOut(out_6[16]));
  Reg1 reg1_18 (.Rd(Rd), .DIn(in_5[17]), .in_4(CLK), .WE(WE), .Sd(Sd), .QOut(out_6[17]));
  Reg1 reg1_19 (.Rd(Rd), .DIn(in_5[18]), .in_4(CLK), .WE(WE), .Sd(Sd), .QOut(out_6[18]));
  Reg1 reg1_20 (.Rd(Rd), .DIn(in_5[19]), .in_4(CLK), .WE(WE), .Sd(Sd), .QOut(out_6[19]));
  Reg1 reg1_21 (.Rd(Rd), .DIn(in_5[20]), .in_4(CLK), .WE(WE), .Sd(Sd), .QOut(out_6[20]));
  Reg1 reg1_22 (.Rd(Rd), .DIn(in_5[21]), .in_4(CLK), .WE(WE), .Sd(Sd), .QOut(out_6[21]));
  Reg1 reg1_23 (.Rd(Rd), .DIn(in_5[22]), .in_4(CLK), .WE(WE), .Sd(Sd), .QOut(out_6[22]));
  Reg1 reg1_24 (.Rd(Rd), .DIn(in_5[23]), .in_4(CLK), .WE(WE), .Sd(Sd), .QOut(out_6[23]));
  Reg1 reg1_25 (.Rd(Rd), .DIn(in_5[24]), .in_4(CLK), .WE(WE), .Sd(Sd), .QOut(out_6[24]));
  Reg1 reg1_26 (.Rd(Rd), .DIn(in_5[25]), .in_4(CLK), .WE(WE), .Sd(Sd), .QOut(out_6[25]));
  Reg1 reg1_27 (.Rd(Rd), .DIn(in_5[26]), .in_4(CLK), .WE(WE), .Sd(Sd), .QOut(out_6[26]));
  Reg1 reg1_28 (.Rd(Rd), .DIn(in_5[27]), .in_4(CLK), .WE(WE), .Sd(Sd), .QOut(out_6[27]));
  Reg1 reg1_29 (.Rd(Rd), .DIn(in_5[28]), .in_4(CLK), .WE(WE), .Sd(Sd), .QOut(out_6[28]));
  Reg1 reg1_30 (.Rd(Rd), .DIn(in_5[29]), .in_4(CLK), .WE(WE), .Sd(Sd), .QOut(out_6[29]));
  Reg1 reg1_31 (.Rd(Rd), .DIn(in_5[30]), .in_4(CLK), .WE(WE), .Sd(Sd), .QOut(out_6[30]));
  Reg1 reg1_32 (.Rd(Rd), .DIn(in_5[31]), .in_4(CLK), .WE(WE), .Sd(Sd), .QOut(out_6[31]));

  // Notes on the sheet:
  //   DataIn
  //   DataOut
endmodule

module RegFile (
  input  CLK,
  input  [31:0] in_2,
  input  [1:0] R1,
  input  Reset,
  input  WE,
  input  [1:0] W_num,
  input  [1:0] R2,
  output [31:0] out_8,
  output [31:0] out_9
);

  wire decoder_1_out1, decoder_1_out2, decoder_1_out3;
  wire [31:0] reg32_1_out_6, reg32_2_out_6, reg32_3_out_6;

  Decoder #(.select(2), .tristate("false"), .disabled(0), .enable("true")) decoder_1 (
    .out1(decoder_1_out1), .out2(decoder_1_out2), .out3(decoder_1_out3), .sel(W_num), .en(WE));  // open: out0
  Reg32 reg32_1 (.WE(decoder_1_out1), .Rd(Reset), .CLK(CLK), .in_5(in_2), .out_6(reg32_1_out_6), .Sd(decoder_1_out1));
  Reg32 reg32_2 (.WE(decoder_1_out2), .Rd(Reset), .CLK(CLK), .in_5(in_2), .out_6(reg32_2_out_6), .Sd(decoder_1_out2));
  Reg32 reg32_3 (.WE(decoder_1_out3), .Rd(Reset), .CLK(CLK), .in_5(in_2), .out_6(reg32_3_out_6), .Sd(decoder_1_out3));
  Multiplexer #(.select(2), .width(32), .disabled("Z"), .enable("false")) multiplexer_1 (
    .in0({32{1'b0}}), .in1(reg32_1_out_6), .in2(reg32_2_out_6), .in3(reg32_3_out_6), .out(out_8), .sel(R1));
  Multiplexer #(.select(2), .width(32), .disabled("Z"), .enable("false")) multiplexer_2 (
    .in0({32{1'b0}}), .in1(reg32_1_out_6), .in2(reg32_2_out_6), .in3(reg32_3_out_6), .out(out_9), .sel(R2));

  // Notes on the sheet:
  //   Din
  //   RD2
  //   RD1
endmodule
