// Logisim project lab_9.circ as structural Verilog
module ALU32 (
  input  [31:0] in_1,
  input  in_2,
  input  in_3,
  input  [1:0] in_4,
  input  [31:0] in_5,
  input  Binvert,
  output [31:0] out_7,
  output Overflow
);

  wire alu1_1_carryout, alu1_2_carryout, alu1_3_carryout, alu1_4_carryout, alu1_5_carryout, alu1_6_carryout,
       alu1_7_carryout, alu1_8_carryout, alu1_9_carryout, alu1_10_carryout, alu1_11_carryout,
       alu1_12_carryout, alu1_13_carryout, alu1_14_carryout, alu1_15_carryout, alu1_16_carryout,
       alu1_17_carryout, alu1_18_carryout, alu1_19_carryout, alu1_20_carryout, alu1_21_carryout,
       alu1_22_carryout, alu1_23_carryout, alu1_24_carryout, alu1_25_carryout, alu1_26_carryout,
       alu1_27_carryout, alu1_28_carryout, alu1_29_carryout, alu1_30_carryout, alu1_31_carryout, Less;

  ALU1 alu1_1 (
    .a(in_1[0]), .Ainvert(in_2), .Less(Less), .b(in_5[0]), .Operation(in_4), .CarryIn(in_3),
    .Binvert(Binvert), .Result(out_7[0]), .CarryOut(alu1_1_carryout));
  ALU1 alu1_2 (
    .a(in_1[1]), .Ainvert(in_2), .Less(1'b0), .b(in_5[1]), .Operation(in_4), .CarryIn(alu1_1_carryout),
    .Binvert(Binvert), .Result(out_7[1]), .CarryOut(alu1_2_carryout));
  ALU1 alu1_3 (
    .a(in_1[2]), .Ainvert(in_2), .Less(1'b0), .b(in_5[2]), .Operation(in_4), .CarryIn(alu1_2_carryout),
    .Binvert(Binvert), .Result(out_7[2]), .CarryOut(alu1_3_carryout));
  ALU1 alu1_4 (
    .a(in_1[3]), .Ainvert(in_2), .Less(1'b0), .b(in_5[3]), .Operation(in_4), .CarryIn(alu1_3_carryout),
    .Binvert(Binvert), .Result(out_7[3]), .CarryOut(alu1_4_carryout));
  ALU1 alu1_5 (
    .a(in_1[4]), .Ainvert(in_2), .Less(1'b0), .b(in_5[4]), .Operation(in_4), .CarryIn(alu1_4_carryout),
    .Binvert(Binvert), .Result(out_7[4]), .CarryOut(alu1_5_carryout));
  ALU1 alu1_6 (
    .a(in_1[5]), .Ainvert(in_2), .Less(1'b0), .b(in_5[5]), .Operation(in_4), .CarryIn(alu1_5_carryout),
    .Binvert(Binvert), .Result(out_7[5]), .CarryOut(alu1_6_carryout));
  ALU1 alu1_7 (
    .a(in_1[6]), .Ainvert(in_2), .Less(1'b0), .b(in_5[6]), .Operation(in_4), .CarryIn(alu1_6_carryout),
    .Binvert(Binvert), .Result(out_7[6]), .CarryOut(alu1_7_carryout));
  ALU1 alu1_8 (
    .a(in_1[7]), .Ainvert(in_2), .Less(1'b0), .b(in_5[7]), .Operation(in_4), .CarryIn(alu1_7_carryout),
    .Binvert(Binvert), .Result(out_7[7]), .CarryOut(alu1_8_carryout));
  ALU1 alu1_9 (
    .a(in_1[8]), .Ainvert(in_2), .Less(1'b0), .b(in_5[8]), .Operation(in_4), .CarryIn(alu1_8_carryout),
    .Binvert(Binvert), .Result(out_7[8]), .CarryOut(alu1_9_carryout));
  ALU1 alu1_10 (
    .a(in_1[9]), .Ainvert(in_2), .Less(1'b0), .b(in_5[9]), .Operation(in_4), .CarryIn(alu1_9_carryout),
    .Binvert(Binvert), .Result(out_7[9]), .CarryOut(alu1_10_carryout));
  ALU1 alu1_11 (
    .a(in_1[10]), .Ainvert(in_2), .Less(1'b0), .b(in_5[10]), .Operation(in_4), .CarryIn(alu1_10_carryout),
    .Binvert(Binvert), .Result(out_7[10]), .CarryOut(alu1_11_carryout));
  ALU1 alu1_12 (
    .a(in_1[11]), .Ainvert(in_2), .Less(1'b0), .b(in_5[11]), .Operation(in_4), .CarryIn(alu1_11_carryout),
    .Binvert(Binvert), .Result(out_7[11]), .CarryOut(alu1_12_carryout));
  ALU1 alu1_13 (
    .a(in_1[12]), .Ainvert(in_2), .Less(1'b0), .b(in_5[12]), .Operation(in_4), .CarryIn(alu1_12_carryout),
    .Binvert(Binvert), .Result(out_7[12]), .CarryOut(alu1_13_carryout));
  ALU1 alu1_14 (
    .a(in_1[13]), .Ainvert(in_2), .Less(1'b0), .b(in_5[13]), .Operation(in_4), .CarryIn(alu1_13_carryout),
    .Binvert(Binvert), .Result(out_7[13]), .CarryOut(alu1_14_carryout));
  ALU1 alu1_15 (
    .a(in_1[14]), .Ainvert(in_2), .Less(1'b0), .b(in_5[14]), .Operation(in_4), .CarryIn(alu1_14_carryout),
    .Binvert(Binvert), .Result(out_7[14]), .CarryOut(alu1_15_carryout));
  ALU1 alu1_16 (
    .a(in_1[15]), .Ainvert(in_2), .Less(1'b0), .b(in_5[15]), .Operation(in_4), .CarryIn(alu1_15_carryout),
    .Binvert(Binvert), .Result(out_7[15]), .CarryOut(alu1_16_carryout));
  ALU1 alu1_17 (
    .a(in_1[16]), .Ainvert(in_2), .Less(1'b0), .b(in_5[16]), .Operation(in_4), .CarryIn(alu1_16_carryout),
    .Binvert(Binvert), .Result(out_7[16]), .CarryOut(alu1_17_carryout));
  ALU1 alu1_18 (
    .a(in_1[17]), .Ainvert(in_2), .Less(1'b0), .b(in_5[17]), .Operation(in_4), .CarryIn(alu1_17_carryout),
    .Binvert(Binvert), .Result(out_7[17]), .CarryOut(alu1_18_carryout));
  ALU1 alu1_19 (
    .a(in_1[18]), .Ainvert(in_2), .Less(1'b0), .b(in_5[18]), .Operation(in_4), .CarryIn(alu1_18_carryout),
    .Binvert(Binvert), .Result(out_7[18]), .CarryOut(alu1_19_carryout));
  ALU1 alu1_20 (
    .a(in_1[19]), .Ainvert(in_2), .Less(1'b0), .b(in_5[19]), .Operation(in_4), .CarryIn(alu1_19_carryout),
    .Binvert(Binvert), .Result(out_7[19]), .CarryOut(alu1_20_carryout));
  ALU1 alu1_21 (
    .a(in_1[20]), .Ainvert(in_2), .Less(1'b0), .b(in_5[20]), .Operation(in_4), .CarryIn(alu1_20_carryout),
    .Binvert(Binvert), .Result(out_7[20]), .CarryOut(alu1_21_carryout));
  ALU1 alu1_22 (
    .a(in_1[21]), .Ainvert(in_2), .Less(1'b0), .b(in_5[21]), .Operation(in_4), .CarryIn(alu1_21_carryout),
    .Binvert(Binvert), .Result(out_7[21]), .CarryOut(alu1_22_carryout));
  ALU1 alu1_23 (
    .a(in_1[22]), .Ainvert(in_2), .Less(1'b0), .b(in_5[22]), .Operation(in_4), .CarryIn(alu1_22_carryout),
    .Binvert(Binvert), .Result(out_7[22]), .CarryOut(alu1_23_carryout));
  ALU1 alu1_24 (
    .a(in_1[23]), .Ainvert(in_2), .Less(1'b0), .b(in_5[23]), .Operation(in_4), .CarryIn(alu1_23_carryout),
    .Binvert(Binvert), .Result(out_7[23]), .CarryOut(alu1_24_carryout));
  ALU1 alu1_25 (
    .a(in_1[24]), .Ainvert(in_2), .Less(1'b0), .b(in_5[24]), .Operation(in_4), .CarryIn(alu1_24_carryout),
    .Binvert(Binvert), .Result(out_7[24]), .CarryOut(alu1_25_carryout));
  ALU1 alu1_26 (
    .a(in_1[25]), .Ainvert(in_2), .Less(1'b0), .b(in_5[25]), .Operation(in_4), .CarryIn(alu1_25_carryout),
    .Binvert(Binvert), .Result(out_7[25]), .CarryOut(alu1_26_carryout));
  ALU1 alu1_27 (
    .a(in_1[26]), .Ainvert(in_2), .Less(1'b0), .b(in_5[26]), .Operation(in_4), .CarryIn(alu1_26_carryout),
    .Binvert(Binvert), .Result(out_7[26]), .CarryOut(alu1_27_carryout));
  ALU1 alu1_28 (
    .a(in_1[27]), .Ainvert(in_2), .Less(1'b0), .b(in_5[27]), .Operation(in_4), .CarryIn(alu1_27_carryout),
    .Binvert(Binvert), .Result(out_7[27]), .CarryOut(alu1_28_carryout));
  ALU1 alu1_29 (
    .a(in_1[28]), .Ainvert(in_2), .Less(1'b0), .b(in_5[28]), .Operation(in_4), .CarryIn(alu1_28_carryout),
    .Binvert(Binvert), .Result(out_7[28]), .CarryOut(alu1_29_carryout));
  ALU1 alu1_30 (
    .a(in_1[29]), .Ainvert(in_2), .Less(1'b0), .b(in_5[29]), .Operation(in_4), .CarryIn(alu1_29_carryout),
    .Binvert(Binvert), .Result(out_7[29]), .CarryOut(alu1_30_carryout));
  ALU1 alu1_31 (
    .a(in_1[30]), .Ainvert(in_2), .Less(1'b0), .b(in_5[30]), .Operation(in_4), .CarryIn(alu1_30_carryout),
    .Binvert(Binvert), .Result(out_7[30]), .CarryOut(alu1_31_carryout));
  ALU31 alu31_1 (
    .a(in_1[31]), .Ainvert(in_2), .Less(1'b0), .Operation(in_4), .b(in_5[31]), .CarryIn(alu1_31_carryout),
    .Binvert(Binvert), .Result(out_7[31]), .Overflow(Overflow), .Set(Less));  // open: out_11

  // Other names for the same wires on the sheet: Ainvert = in_2; CarryIn = in_3; A0 = in_1[0]; A1 = in_1[1];
  //   A2 = in_1[2]; A3 = in_1[3]; A4 = in_1[4]; A5 = in_1[5]; A6 = in_1[6]; A7 = in_1[7]; A8 = in_1[8]; A9 = in_1[9];
  //   A10 = in_1[10]; A11 = in_1[11]; A12 = in_1[12]; A13 = in_1[13]; A14 = in_1[14]; A15 = in_1[15]; A16 = in_1[16];
  //   A17 = in_1[17]; A18 = in_1[18]; A19 = in_1[19]; A20 = in_1[20]; A21 = in_1[21]; A22 = in_1[22]; A23 = in_1[23];
  //   A24 = in_1[24]; A25 = in_1[25]; A26 = in_1[26]; A27 = in_1[27]; A28 = in_1[28]; A29 = in_1[29]; A30 = in_1[30];
  //   A31 = in_1[31]; B0 = in_5[0]; B1 = in_5[1]; B2 = in_5[2]; B3 = in_5[3]; B4 = in_5[4]; B5 = in_5[5];
  //   B6 = in_5[6]; B7 = in_5[7]; B8 = in_5[8]; B9 = in_5[9]; B10 = in_5[10]; B11 = in_5[11]; B12 = in_5[12];
  //   B13 = in_5[13]; B14 = in_5[14]; B15 = in_5[15]; B16 = in_5[16]; B17 = in_5[17]; B18 = in_5[18]; B19 = in_5[19];
  //   B20 = in_5[20]; B21 = in_5[21]; B22 = in_5[22]; B23 = in_5[23]; B24 = in_5[24]; B25 = in_5[25]; B26 = in_5[26];
  //   B27 = in_5[27]; B28 = in_5[28]; B29 = in_5[29]; B30 = in_5[30]; B31 = in_5[31]; Operation[1:0] = in_4;
  //   R0 = out_7[0]; R1 = out_7[1]; R2 = out_7[2]; R3 = out_7[3]; R4 = out_7[4]; R5 = out_7[5]; R6 = out_7[6];
  //   R7 = out_7[7]; R8 = out_7[8]; R9 = out_7[9]; R10 = out_7[10]; R11 = out_7[11]; R12 = out_7[12]; R13 = out_7[13];
  //   R14 = out_7[14]; R15 = out_7[15]; R16 = out_7[16]; R17 = out_7[17]; R18 = out_7[18]; R19 = out_7[19];
  //   R20 = out_7[20]; R21 = out_7[21]; R22 = out_7[22]; R23 = out_7[23]; R24 = out_7[24]; R25 = out_7[25];
  //   R26 = out_7[26]; R27 = out_7[27]; R28 = out_7[28]; R29 = out_7[29]; R30 = out_7[30]; R31 = out_7[31]

  // Notes on the sheet:
  //   A
  //   Ainvert
  //   CarryIn
  //   Operation
  //   B
  //   Result
endmodule

module ALU1 (
  input  a,
  input  Ainvert,
  input  Less,
  input  b,
  input  [1:0] Operation,
  input  CarryIn,
  input  Binvert,
  output Result,
  output CarryOut
);

  wire adder_1_out, and_1_out, multiplexer_1_out, multiplexer_2_out, not_1_out, not_2_out, or_1_out;

  not not_1 (not_1_out, a);
  not not_2 (not_2_out, b);
  Multiplexer #(.select(1), .width(1), .disabled("Z"), .enable("false")) multiplexer_1 (
    .in0(a), .in1(not_1_out), .out(multiplexer_1_out), .sel(Ainvert));
  Multiplexer #(.select(1), .width(1), .disabled("Z"), .enable("false")) multiplexer_2 (
    .in0(b), .in1(not_2_out), .out(multiplexer_2_out), .sel(Binvert));
  and and_1 (and_1_out, multiplexer_1_out, multiplexer_2_out);
  or or_1 (or_1_out, multiplexer_1_out, multiplexer_2_out);
  Adder #(.width(1)) adder_1 (
    .a(multiplexer_1_out), .b(multiplexer_2_out), .out(adder_1_out), .cin(CarryIn), .cout(CarryOut));
  Multiplexer #(.select(2), .width(1), .disabled("Z"), .enable("false")) multiplexer_3 (
    .in0(and_1_out), .in1(or_1_out), .in2(adder_1_out), .in3(Less), .out(Result), .sel(Operation));
endmodule

module ALU31 (
  input  a,
  input  Ainvert,
  input  Less,
  input  [1:0] Operation,
  input  b,
  input  CarryIn,
  input  Binvert,
  output Result,
  output Overflow,
  output Set,
  output out_11
);

  wire and_1_out, multiplexer_1_out, multiplexer_2_out, not_1_out, not_2_out, or_1_out;

  not not_1 (not_1_out, a);
  not not_2 (not_2_out, b);
  Multiplexer #(.select(1), .width(1), .disabled("Z"), .enable("false")) multiplexer_1 (
    .in0(a), .in1(not_1_out), .out(multiplexer_1_out), .sel(Ainvert));
  Multiplexer #(.select(1), .width(1), .disabled("Z"), .enable("false")) multiplexer_2 (
    .in0(b), .in1(not_2_out), .out(multiplexer_2_out), .sel(Binvert));
  and and_1 (and_1_out, multiplexer_1_out, multiplexer_2_out);
  or or_1 (or_1_out, multiplexer_1_out, multiplexer_2_out);
  Adder #(.width(1)) adder_1 (.a(multiplexer_1_out), .b(multiplexer_2_out), .out(Set), .cin(CarryIn), .cout(out_11));
  Multiplexer #(.select(2), .width(1), .disabled("Z"), .enable("false")) multiplexer_3 (
    .in0(and_1_out), .in1(or_1_out), .in2(Set), .in3(Less), .out(Result), .sel(Operation));
  xor xor_1 (Overflow, CarryIn, out_11);

  // Notes on the sheet:
  //   CarryOut
endmodule
