// Logisim project MIPS RAM for M-instruction.circ as structural Verilog: 1 circuit, main circuit ◇MIPS RAM
module MIPS_RAM (
  input  [11:0] \字节地址 ,
  input  [31:0] Din,
  input  CLK,
  input  WE,
  input  [1:0] Mode,
  output [31:0] DataOut
);

  wire _00, _01, _10, and_1_out, and_2_out, and_3_out, and_4_out, and_5_out, and_6_out, and_7_out, and_8_out,
       and_9_out, and_10_out, and_11_out, and_12_out, decoder_2_out0, decoder_3_out1, decoder_4_out2,
       decoder_5_out3, not_1_out, not_2_out, w0, w1, w2, w3;
  wire [7:0] byte0, byte1, byte2, byte3, d0, d1, d2, d3, multiplexer_1_out, \计数器_q ;
  wire [15:0] multiplexer_2_out;
  wire [31:0] bit_extender_1_out, bit_extender_2_out;

  and and_1 (and_1_out, WE, w0);
  RAM #(.addrWidth(10), .bus("separate"), .Select("high"), .simpleMode("false")) ram_1 (
    .addr(\字节地址 [11:2]), .din(d0), .data(byte0), .str(and_1_out), .sel(1'b1), .clk(CLK));  // open: ld, clr
  Multiplexer #(.select(2), .width(8), .enable("false")) multiplexer_1 (
    .in0(byte0), .in1(byte1), .in2(byte2), .in3(byte3), .out(multiplexer_1_out), .sel(\字节地址 [1:0]));
  Multiplexer #(.width(16), .enable("false")) multiplexer_2 (
    .in0({byte1, byte0}), .in1({byte3, byte2}), .out(multiplexer_2_out), .sel(\字节地址 [1]));
  Multiplexer #(.select(2), .width(8), .enable("false")) multiplexer_3 (
    .in0(Din[7:0]), .in1(Din[7:0]), .in2(Din[7:0]), .out(d0), .sel(Mode));  // open: in3
  Multiplexer #(.select(2), .width(8), .enable("false")) multiplexer_4 (
    .in0(Din[15:8]), .in1(Din[7:0]), .in2(Din[15:8]), .out(d1), .sel(Mode));  // open: in3
  Multiplexer #(.select(2), .width(8), .enable("false")) multiplexer_5 (
    .in0(Din[23:16]), .in1(Din[7:0]), .in2(Din[7:0]), .out(d2), .sel(Mode));  // open: in3
  Multiplexer #(.select(2), .width(8), .enable("false")) multiplexer_6 (
    .in0(Din[31:24]), .in1(Din[7:0]), .in2(Din[15:8]), .out(d3), .sel(Mode));  // open: in3
  and and_2 (and_2_out, WE, w1);
  assign bit_extender_1_out = {{24{1'b0}}, multiplexer_1_out};  // Bit_Extender bit_extender_1
  assign bit_extender_2_out = {{16{1'b0}}, multiplexer_2_out};  // Bit_Extender bit_extender_2
  RAM #(.addrWidth(10), .bus("separate"), .Select("high"), .simpleMode("false")) ram_2 (
    .addr(\字节地址 [11:2]), .din(d1), .data(byte1), .str(and_2_out), .sel(1'b1), .clk(CLK));  // open: ld, clr
  // Probe on DataOut
  and and_3 (and_3_out, WE, w2);
  Multiplexer #(.select(2), .width(32), .enable("false")) multiplexer_7 (
    .in0({byte3, byte2, byte1, byte0}), .in1(bit_extender_1_out), .in2(bit_extender_2_out), .out(DataOut),
    .sel(Mode));  // open: in3
  RAM #(.addrWidth(10), .bus("separate"), .Select("high"), .simpleMode("false")) ram_3 (
    .addr(\字节地址 [11:2]), .din(d2), .data(byte2), .str(and_3_out), .sel(1'b1), .clk(CLK));  // open: ld, clr
  Counter #(.behavior("old")) \u_计数器  (.Q(\计数器_q ), .clk(CLK));  // open: load, D, count, carry, clr, preset
  // Probe on \计数器_q 
  and and_4 (and_4_out, WE, w3);
  Decoder #(.select(2), .enable("false")) decoder_1 (.out0(_00), .out1(_01), .out2(_10), .sel(Mode));  // open: out3
  Decoder #(.select(2), .enable("false")) decoder_2 (
    .out0(decoder_2_out0), .sel(\字节地址 [1:0]));  // open: out1, out2, out3
  Decoder #(.select(2), .enable("false")) decoder_3 (
    .out1(decoder_3_out1), .sel(\字节地址 [1:0]));  // open: out0, out2, out3
  Decoder #(.select(2), .enable("false")) decoder_4 (
    .out2(decoder_4_out2), .sel(\字节地址 [1:0]));  // open: out0, out1, out3
  Decoder #(.select(2), .enable("false")) decoder_5 (
    .out3(decoder_5_out3), .sel(\字节地址 [1:0]));  // open: out0, out1, out2
  RAM #(.addrWidth(10), .bus("separate"), .Select("high"), .simpleMode("false")) ram_4 (
    .addr(\字节地址 [11:2]), .din(d3), .data(byte3), .str(and_4_out), .sel(1'b1), .clk(CLK));  // open: ld, clr
  and and_5 (and_5_out, _01, decoder_2_out0);
  and and_6 (and_6_out, _10, not_1_out);
  not not_1 (not_1_out, \字节地址 [1]);
  not not_2 (not_2_out, \字节地址 [1]);
  and and_7 (and_7_out, not_2_out, _10);
  and and_8 (and_8_out, _01, decoder_4_out2);
  and and_9 (and_9_out, \字节地址 [1], _10);
  and and_10 (and_10_out, \字节地址 [1], _10);
  and and_11 (and_11_out, _01, decoder_3_out1);
  and and_12 (and_12_out, _01, decoder_5_out3);
  or or_1 (w0, _00, and_5_out, and_6_out);
  or or_2 (w1, _00, and_11_out, and_7_out);
  or or_3 (w2, _00, and_8_out, and_9_out);
  or or_4 (w3, _00, and_12_out, and_10_out);

  // Other names for the same wires on the sheet: Dout[31:0] = DataOut

  // Notes on the sheet:
  //   输入引脚区
  //   请勿增改引脚，请勿修改子电路封装
  //   电路功能：利用下图中给定的RAM器件实现既既可以按照字节，也可以按照半字，也可以按照32位字访问的MIPS存储器
  //   请在下方利用上方输入输出引脚的隧道信号构建电路，ctrl+d复制选择部件
  //   输出引脚区
  //   为方便测试，注意Dout应一直输出数据，所有数据位不得悬空，所有RAM芯片ld控制端悬空即可
endmodule
