// Logisim project 251117.circ as structural Verilog: 15 circuits, main circuit ◇多周期MIPS(微程序)
module \单周期MIPS_硬布线  (
  output RegWrite,
  output MemWrite,
  output [31:0] PC,
  output [31:0] IR,
  output [31:0] RDin,
  output [31:0] MDin
);

  wire Andi, beq_out, bne_out, CLK, mips_alu_1_equal, not_1_out, not_2_out, or_1_out, RST,
       \单周期控制器封装_1_alusrcb , \单周期控制器封装_1_beq , \单周期控制器封装_1_bne , \单周期控制器封装_1_halt , \单周期控制器封装_1_j ,
       \单周期控制器封装_1_memtoreg , \单周期控制器封装_1_regdst ;
  wire [3:0] \单周期控制器封装_1_aluop ;
  wire [4:0] multiplexer_3_out;
  wire [9:0] mips_alu_1_result_2;
  wire [15:0] \总周期数 ;
  wire [27:0] adder_1_out;
  wire [31:0] adder_2_out, bit_extender_1_out, bit_extender_2_out, mips_alu_1_result, mips_regifile_1_r1,
       multiplexer_1_out, multiplexer_2_out, multiplexer_4_out, multiplexer_5_out, ram_1_data, shifter_1_out;
  wire [31:28] adder_1_out_2;

  Button \u_总复位  (.out(RST));
  Multiplexer #(.select(1), .width(32), .disabled("Z"), .enable("false")) multiplexer_1 (
    .in0({adder_1_out_2, adder_1_out}), .in1(adder_2_out), .out(multiplexer_1_out), .sel(or_1_out));
  Clock #(.highDuration(1), .lowDuration(1)) clock_1 (.out(CLK));
  Counter #(.width(16), .max('hffff), .ongoal("wrap"), .trigger("rising"), .behavior("old")) counter_1 (
    .count(not_1_out), .Q(\总周期数 ), .clk(CLK), .clr(RST));  // open: load, D, carry, preset
  Multiplexer #(.select(1), .width(32), .disabled("Z"), .enable("false")) multiplexer_2 (
    .in0(multiplexer_1_out), .in1({adder_1_out_2, IR[25:0], 2'b00}), .out(multiplexer_2_out),
    .sel(\单周期控制器封装_1_j ));
  Register #(.width(32), .trigger("rising"), .Select("low")) u_PC (
    .D(multiplexer_2_out), .en(not_1_out), .Q(PC), .clk(CLK), .clr(RST));
  // Probe on \总周期数 
  // Probe on \总周期数 
  // Mips_Probe mips_probe_1: pin names not known; wires that end beside it: IR
  Adder #(.width(32)) adder_1 (.a(PC), .b(32'h4), .out({adder_1_out_2, adder_1_out}));  // open: cin, cout
  not not_1 (not_1_out, \单周期控制器封装_1_halt );
  ROM #(.addrWidth(10), .dataWidth(32), .Select("high")) rom_1 (.addr(PC[11:2]), .data(IR));
  Adder #(.width(32)) adder_2 (
    .a({adder_1_out_2, adder_1_out}), .b(shifter_1_out), .out(adder_2_out));  // open: cin, cout
  \单周期控制器封装  \u_单周期控制器封装_1  (
    .Andi(Andi), .J(\单周期控制器封装_1_j ), .Halt(\单周期控制器封装_1_halt ), .OP(IR[31:26]), .Funct(IR[5:0]),
    .MemtoReg(\单周期控制器封装_1_memtoreg ), .MemWrite(MemWrite), .Beq(\单周期控制器封装_1_beq ),
    .AluOp(\单周期控制器封装_1_aluop ), .Bne(\单周期控制器封装_1_bne ), .AluSrcB(\单周期控制器封装_1_alusrcb ), .RegWrite(RegWrite),
    .RegDst(\单周期控制器封装_1_regdst ));
  Multiplexer #(.select(1), .width(5), .disabled("Z"), .enable("false")) multiplexer_3 (
    .in0(IR[20:16]), .in1(IR[15:11]), .out(multiplexer_3_out), .sel(\单周期控制器封装_1_regdst ));
  assign bit_extender_1_out = {{16{IR[15]}}, IR[15:0]};  // Bit_Extender bit_extender_1
  assign bit_extender_2_out = {{16{1'b0}}, IR[15:0]};  // Bit_Extender bit_extender_2
  Multiplexer #(.select(1), .width(32), .disabled("Z"), .enable("false")) multiplexer_4 (
    .in0(bit_extender_1_out), .in1(bit_extender_2_out), .out(multiplexer_4_out), .sel(Andi));
  MIPS_Regifile mips_regifile_1 (
    .Din(RDin), .Clk(CLK), .R1(mips_regifile_1_r1), .R2(MDin), .WE(RegWrite), .W_num(multiplexer_3_out),
    .R1_num(IR[25:21]), .R2_num(IR[20:16]));
  Multiplexer #(.select(1), .width(32), .disabled("Z"), .enable("false")) multiplexer_5 (
    .in0(MDin), .in1(multiplexer_4_out), .out(multiplexer_5_out), .sel(\单周期控制器封装_1_alusrcb ));
  Shifter #(.width(32), .shift("ll")) shifter_1 (.in(bit_extender_1_out), .\dist (5'b00010), .out(shifter_1_out));
  MIPS_ALU mips_alu_1 (
    .X(mips_regifile_1_r1), .Y(multiplexer_5_out), .AluOP(\单周期控制器封装_1_aluop ), .Equal(mips_alu_1_equal),
    .Result({mips_alu_1_result[31:12], mips_alu_1_result_2, mips_alu_1_result[1:0]}));  // open: Result_2
  not not_2 (not_2_out, mips_alu_1_equal);
  and bne (bne_out, \单周期控制器封装_1_bne , not_2_out);
  and beq (beq_out, mips_alu_1_equal, \单周期控制器封装_1_beq );
  or or_1 (or_1_out, beq_out, bne_out);
  RAM #(.addrWidth(10), .dataWidth(32), .bus("separate"), .Select("high")) ram_1 (
    .addr(mips_alu_1_result_2), .din(MDin), .data(ram_1_data), .str(MemWrite), .clk(CLK), .clr(RST));  // open: sel, ld
  Multiplexer #(.select(1), .width(32), .disabled("Z"), .enable("false")) multiplexer_6 (
    .in0({mips_alu_1_result[31:12], mips_alu_1_result_2, mips_alu_1_result[1:0]}), .in1(ram_1_data),
    .out(RDin), .sel(\单周期控制器封装_1_memtoreg ));

  // Notes on the sheet:
  //   程序运行结束后可停机，查看数据存储器中80单元的排序情况是有符号降序
  //   总周期数参考值：224
  //   指令存储器
  //   contents of rom_1 (hex, n*v repeats v):
  //   8000c04 20110000 20090001 ae290200 2002000a c
  //   Halt
  //   J
  //   Op
  //   Func
  //   MemToReg
  //   MemWrite
  //   Beq
  //   Bne
  //   AluOP
  //   AluSrcB
  //   RegWrite
  //   RegDst
  //   为方便自动评测，需要输出PC，IR，寄存器文件写入端口RDin，内存写入端口MDin等信号
endmodule

// 单周期硬布线控制器
module \单周期硬布线控制器  (
  input  [5:0] OP,
  input  [5:0] Func,
  output [3:0] ALU_OP,
  output RegDst,
  output RegWrite,
  output MemToReg,
  output MemWrite,
  output AluSrc,
  output Beq,
  output Bne,
  output Halt
);

  wire ADD, ADDI, comparator_6_eq, comparator_7_eq, comparator_8_eq, comparator_9_eq, comparator_10_eq,
       comparator_11_eq, comparator_12_eq, comparator_13_eq, comparator_14_eq, controlled_buffer_1_out,
       or_4_out, SLT;

  Comparator #(.width(6), .mode("twosComplement")) comparator_1 (.a(OP), .b(6'b100011), .eq(MemToReg));  // open: gt, lt
  Comparator #(.width(6), .mode("twosComplement")) comparator_2 (.a(OP), .b(6'b101011), .eq(MemWrite));  // open: gt, lt
  Comparator #(.width(6), .mode("twosComplement")) comparator_3 (.a(OP), .b(6'b000100), .eq(Beq));  // open: gt, lt
  Comparator #(.width(6), .mode("twosComplement")) comparator_4 (.a(OP), .b(6'b000101), .eq(Bne));  // open: gt, lt
  Comparator #(.width(6), .mode("twosComplement")) comparator_5 (.a(OP), .b(6'b001000), .eq(ADDI));  // open: gt, lt
  Comparator #(.width(6), .mode("twosComplement")) comparator_6 (
    .a(OP), .b({6{1'b0}}), .eq(comparator_6_eq));  // open: gt, lt
  Comparator #(.width(6), .mode("twosComplement")) comparator_7 (
    .a(Func), .b(6'b100000), .eq(comparator_7_eq));  // open: gt, lt
  Comparator #(.width(6), .mode("twosComplement")) comparator_8 (
    .a(Func), .b(6'b101010), .eq(comparator_8_eq));  // open: gt, lt
  Comparator #(.width(6), .mode("twosComplement")) comparator_9 (
    .a(Func), .b(6'b001100), .eq(comparator_9_eq));  // open: gt, lt
  or or_1 (RegWrite, MemToReg, ADDI, RegDst);
  or or_2 (RegDst, SLT, ADD);
  and and_1 (ADD, comparator_7_eq, comparator_6_eq);
  and and_2 (SLT, comparator_8_eq, comparator_6_eq);
  and and_3 (Halt, comparator_9_eq, comparator_6_eq);
  or or_3 (AluSrc, MemWrite, MemToReg, ADDI);
  Comparator #(.width(6), .mode("twosComplement")) comparator_10 (
    .a(OP), .b(6'b100011), .eq(comparator_10_eq));  // open: gt, lt
  Comparator #(.width(6), .mode("twosComplement")) comparator_11 (
    .a(OP), .b(6'b101011), .eq(comparator_11_eq));  // open: gt, lt
  Comparator #(.width(6), .mode("twosComplement")) comparator_12 (
    .a(OP), .b(6'b001000), .eq(comparator_12_eq));  // open: gt, lt
  Comparator #(.width(6), .mode("twosComplement")) comparator_13 (
    .a(OP), .b({6{1'b0}}), .eq(comparator_13_eq));  // open: gt, lt
  Comparator #(.width(6), .mode("twosComplement")) comparator_14 (
    .a(Func), .b(6'b100000), .eq(comparator_14_eq));  // open: gt, lt
  assign controlled_buffer_1_out = comparator_13_eq ? comparator_14_eq : 1'bz;  // Controlled_Buffer controlled_buffer_1
  assign ALU_OP = ~or_4_out ? 4'b1011 : 4'bz;  // Controlled_Buffer controlled_buffer_2
  assign ALU_OP = or_4_out ? 4'b0101 : 4'bz;  // Controlled_Buffer controlled_buffer_3
  or or_4 (or_4_out, comparator_10_eq, comparator_11_eq, comparator_12_eq, controlled_buffer_1_out);

  // Other names for the same wires on the sheet: LW = MemToReg; R_TYPE = RegDst; SW = MemWrite; SysCall = Halt

  // Notes on the sheet:
  //   指令译码信号
  //   指令译码逻辑
  //   给出简单的逻辑实现对应指令译码信号，LW、SW、BEQ、BNE、ADDI、ADD、SLT、SYSCALL、R_TYPE。
  //   ALU控制器逻辑
  //   注意R_TYPE表示R型运算指令，SYSCALL是特殊的R型指令，不属于这个类别
  //   根据指令译码信号实现控制器输出控制信号的逻辑
  //   给出简单的逻辑实现ALU_OP与OP、Func之间的对应关系
  //   控制信号
endmodule

module \单周期万能表格法控制器  (
  input  OP5,
  input  OP4,
  input  OP3,
  input  OP2,
  input  OP1,
  input  OP0,
  input  F5,
  input  F4,
  input  F3,
  input  F2,
  input  F1,
  input  F0,
  output Andi,
  output Halt,
  output Jump,
  output MemtoReg,
  output Memwrite,
  output Beq,
  output Bne,
  output s3,
  output s2,
  output s1,
  output s0,
  output AluSrcB,
  output Regwrite,
  output RegDst
);

  wire and_8_out, and_9_out, and_10_out, and_11_out, and_12_out, and_13_out, and_14_out, and_15_out,
       and_16_out, and_17_out, and_18_out, and_19_out, and_20_out, and_21_out, and_22_out, and_23_out,
       and_24_out, and_25_out, and_26_out, and_27_out, and_28_out, and_29_out, and_30_out, and_31_out,
       and_32_out, and_33_out, and_34_out, and_35_out, and_36_out, and_37_out, and_38_out, and_39_out,
       and_40_out, and_41_out, and_42_out, and_43_out, not_1_out, not_2_out, not_3_out, not_4_out, not_5_out,
       not_6_out, not_7_out, not_8_out, not_9_out, not_10_out, not_11_out, not_12_out, not_13_out,
       not_14_out, not_15_out, not_16_out, not_17_out, not_18_out, not_19_out, not_20_out, not_21_out,
       not_22_out, not_23_out, not_24_out, not_25_out, not_26_out, not_27_out, not_28_out, not_29_out,
       not_30_out, not_31_out, not_32_out, not_33_out, not_34_out, not_35_out, not_36_out, not_37_out,
       not_38_out, not_39_out, not_40_out, not_41_out, not_42_out, not_43_out, not_44_out, not_45_out,
       not_46_out, not_47_out, not_48_out, not_49_out, not_50_out, not_51_out, not_52_out, not_53_out,
       not_54_out, not_55_out, not_56_out, not_57_out, not_58_out, not_59_out, not_60_out, not_61_out,
       not_62_out, not_63_out, not_64_out, not_65_out, not_66_out, not_67_out, not_68_out, not_69_out,
       not_70_out, not_71_out, not_72_out, not_73_out, not_74_out, not_75_out, not_76_out, not_77_out,
       not_78_out, not_79_out, not_80_out, not_81_out, not_82_out, not_83_out, not_84_out, not_85_out,
       not_86_out, not_87_out, not_88_out, not_89_out, not_90_out, not_91_out, not_92_out, not_93_out,
       not_94_out, not_95_out, not_96_out, not_97_out, not_98_out, not_99_out, not_100_out, not_101_out,
       not_102_out, not_103_out, not_104_out, not_105_out, not_106_out, not_107_out, not_108_out,
       not_109_out, not_110_out, not_111_out, not_112_out, not_113_out, not_114_out, not_115_out,
       not_116_out, not_117_out, not_118_out, not_119_out, not_120_out, not_121_out, not_122_out,
       not_123_out, not_124_out, not_125_out, not_126_out, not_127_out, not_128_out, not_129_out,
       not_130_out, not_131_out, not_132_out, not_133_out, not_134_out, not_135_out, not_136_out,
       not_137_out, not_138_out, not_139_out, not_140_out, not_141_out, not_142_out, not_143_out,
       not_144_out, not_145_out, not_146_out, not_147_out, not_148_out, not_149_out, not_150_out,
       not_151_out, not_152_out, not_153_out, not_154_out, not_155_out, not_156_out, not_157_out,
       not_158_out, not_159_out, not_160_out, not_161_out, not_162_out, not_163_out, not_164_out,
       not_165_out, not_166_out, not_167_out, not_168_out, not_169_out, not_170_out, not_171_out,
       not_172_out, not_173_out, not_174_out, not_175_out, not_176_out, not_177_out, not_178_out,
       not_179_out, not_180_out, not_181_out, not_182_out, not_183_out, not_184_out, not_185_out,
       not_186_out, not_187_out, not_188_out, not_189_out, not_190_out, not_191_out, not_192_out,
       not_193_out, not_194_out, not_195_out, not_196_out, not_197_out, not_198_out, not_199_out,
       not_200_out, not_201_out, not_202_out, not_203_out, not_204_out, not_205_out, not_206_out,
       not_207_out, not_208_out, not_209_out, not_210_out, not_211_out, not_212_out, not_213_out,
       not_214_out, not_215_out, not_216_out, not_217_out, not_218_out, not_219_out, not_220_out,
       not_221_out, not_222_out, not_223_out, not_224_out, not_225_out, not_226_out, not_227_out,
       not_228_out, not_229_out, not_230_out, not_231_out, not_232_out, not_233_out, not_234_out,
       not_235_out, not_236_out, not_237_out, not_238_out, not_239_out, not_240_out, not_241_out,
       not_242_out, not_243_out, not_244_out, not_245_out, not_246_out, not_247_out, not_248_out,
       not_249_out, not_250_out, not_251_out, not_252_out, not_253_out, not_254_out, not_255_out,
       not_256_out, not_257_out;

  not not_1 (not_1_out, OP5);
  not not_2 (not_2_out, OP4);
  not not_3 (not_3_out, OP1);
  not not_4 (not_4_out, OP0);
  not not_5 (not_5_out, OP5);
  not not_6 (not_6_out, OP4);
  not not_7 (not_7_out, OP3);
  not not_8 (not_8_out, OP2);
  not not_9 (not_9_out, OP1);
  not not_10 (not_10_out, OP0);
  not not_11 (not_11_out, F5);
  not not_12 (not_12_out, F4);
  not not_13 (not_13_out, F1);
  not not_14 (not_14_out, F0);
  not not_15 (not_15_out, OP5);
  not not_16 (not_16_out, OP4);
  not not_17 (not_17_out, OP3);
  not not_18 (not_18_out, OP2);
  not not_19 (not_19_out, OP0);
  not not_20 (not_20_out, OP4);
  not not_21 (not_21_out, OP3);
  not not_22 (not_22_out, OP2);
  not not_23 (not_23_out, OP4);
  not not_24 (not_24_out, OP2);
  not not_25 (not_25_out, OP5);
  not not_26 (not_26_out, OP4);
  not not_27 (not_27_out, OP3);
  not not_28 (not_28_out, OP1);
  not not_29 (not_29_out, OP0);
  not not_30 (not_30_out, OP5);
  not not_31 (not_31_out, OP4);
  not not_32 (not_32_out, OP3);
  not not_33 (not_33_out, OP1);
  not not_34 (not_34_out, OP5);
  not not_35 (not_35_out, OP4);
  not not_36 (not_36_out, OP3);
  not not_37 (not_37_out, OP2);
  not not_38 (not_38_out, OP1);
  not not_39 (not_39_out, OP0);
  not not_40 (not_40_out, F4);
  not not_41 (not_41_out, F2);
  not not_42 (not_42_out, F0);
  not not_43 (not_43_out, OP5);
  not not_44 (not_44_out, OP4);
  not not_45 (not_45_out, OP3);
  not not_46 (not_46_out, OP1);
  not not_47 (not_47_out, OP0);
  not not_48 (not_48_out, OP5);
  not not_49 (not_49_out, OP4);
  not not_50 (not_50_out, OP3);
  not not_51 (not_51_out, OP1);
  not not_52 (not_52_out, OP5);
  not not_53 (not_53_out, OP4);
  not not_54 (not_54_out, OP3);
  not not_55 (not_55_out, OP2);
  not not_56 (not_56_out, OP1);
  not not_57 (not_57_out, OP0);
  not not_58 (not_58_out, F4);
  not not_59 (not_59_out, F3);
  not not_60 (not_60_out, F2);
  not not_61 (not_61_out, F1);
  not not_62 (not_62_out, F0);
  not not_63 (not_63_out, OP5);
  not not_64 (not_64_out, OP4);
  not not_65 (not_65_out, OP2);
  not not_66 (not_66_out, OP1);
  not not_67 (not_67_out, OP0);
  not not_68 (not_68_out, OP4);
  not not_69 (not_69_out, OP3);
  not not_70 (not_70_out, OP2);
  not not_71 (not_71_out, OP4);
  not not_72 (not_72_out, OP2);
  not not_73 (not_73_out, OP5);
  not not_74 (not_74_out, OP4);
  not not_75 (not_75_out, OP1);
  not not_76 (not_76_out, OP0);
  not not_77 (not_77_out, OP5);
  not not_78 (not_78_out, OP4);
  not not_79 (not_79_out, OP3);
  not not_80 (not_80_out, OP2);
  not not_81 (not_81_out, OP1);
  not not_82 (not_82_out, OP0);
  not not_83 (not_83_out, F4);
  not not_84 (not_84_out, F3);
  not not_85 (not_85_out, F1);
  not not_86 (not_86_out, F0);
  not not_87 (not_87_out, OP5);
  not not_88 (not_88_out, OP4);
  not not_89 (not_89_out, OP3);
  not not_90 (not_90_out, OP2);
  not not_91 (not_91_out, OP1);
  not not_92 (not_92_out, OP0);
  not not_93 (not_93_out, F4);
  not not_94 (not_94_out, F2);
  not not_95 (not_95_out, F0);
  not not_96 (not_96_out, OP5);
  not not_97 (not_97_out, OP4);
  not not_98 (not_98_out, OP3);
  not not_99 (not_99_out, OP1);
  not not_100 (not_100_out, OP0);
  not not_101 (not_101_out, OP5);
  not not_102 (not_102_out, OP4);
  not not_103 (not_103_out, OP3);
  not not_104 (not_104_out, OP1);
  not not_105 (not_105_out, OP5);
  not not_106 (not_106_out, OP4);
  not not_107 (not_107_out, OP1);
  not not_108 (not_108_out, OP0);
  not not_109 (not_109_out, OP5);
  not not_110 (not_110_out, OP4);
  not not_111 (not_111_out, OP3);
  not not_112 (not_112_out, OP2);
  not not_113 (not_113_out, OP1);
  not not_114 (not_114_out, OP0);
  not not_115 (not_115_out, F4);
  not not_116 (not_116_out, F3);
  not not_117 (not_117_out, F1);
  not not_118 (not_118_out, F0);
  not not_119 (not_119_out, OP5);
  not not_120 (not_120_out, OP4);
  not not_121 (not_121_out, OP3);
  not not_122 (not_122_out, OP2);
  not not_123 (not_123_out, OP1);
  not not_124 (not_124_out, OP0);
  not not_125 (not_125_out, F4);
  not not_126 (not_126_out, F3);
  not not_127 (not_127_out, F2);
  not not_128 (not_128_out, F1);
  not not_129 (not_129_out, F0);
  not not_130 (not_130_out, OP5);
  not not_131 (not_131_out, OP4);
  not not_132 (not_132_out, OP3);
  not not_133 (not_133_out, OP2);
  not not_134 (not_134_out, OP1);
  not not_135 (not_135_out, OP0);
  not not_136 (not_136_out, F4);
  not not_137 (not_137_out, F2);
  not not_138 (not_138_out, F0);
  not not_139 (not_139_out, OP5);
  not not_140 (not_140_out, OP4);
  not not_141 (not_141_out, OP2);
  not not_142 (not_142_out, OP1);
  not not_143 (not_143_out, OP0);
  not not_144 (not_144_out, OP5);
  not not_145 (not_145_out, OP4);
  not not_146 (not_146_out, OP3);
  not not_147 (not_147_out, OP1);
  not not_148 (not_148_out, OP0);
  not not_149 (not_149_out, OP5);
  not not_150 (not_150_out, OP4);
  not not_151 (not_151_out, OP3);
  not not_152 (not_152_out, OP1);
  not not_153 (not_153_out, OP4);
  not not_154 (not_154_out, OP3);
  not not_155 (not_155_out, OP2);
  not not_156 (not_156_out, OP4);
  not not_157 (not_157_out, OP2);
  not not_158 (not_158_out, OP5);
  not not_159 (not_159_out, OP4);
  not not_160 (not_160_out, OP1);
  not not_161 (not_161_out, OP0);
  not not_162 (not_162_out, OP5);
  not not_163 (not_163_out, OP4);
  not not_164 (not_164_out, OP3);
  not not_165 (not_165_out, OP2);
  not not_166 (not_166_out, OP1);
  not not_167 (not_167_out, OP0);
  not not_168 (not_168_out, F4);
  not not_169 (not_169_out, F3);
  not not_170 (not_170_out, F1);
  not not_171 (not_171_out, F0);
  not not_172 (not_172_out, OP5);
  not not_173 (not_173_out, OP4);
  not not_174 (not_174_out, OP2);
  not not_175 (not_175_out, OP1);
  not not_176 (not_176_out, OP0);
  not not_177 (not_177_out, OP4);
  not not_178 (not_178_out, OP3);
  not not_179 (not_179_out, OP2);
  not not_180 (not_180_out, OP4);
  not not_181 (not_181_out, OP2);
  not not_182 (not_182_out, OP5);
  not not_183 (not_183_out, OP4);
  not not_184 (not_184_out, OP1);
  not not_185 (not_185_out, OP0);
  not not_186 (not_186_out, OP5);
  not not_187 (not_187_out, OP4);
  not not_188 (not_188_out, OP3);
  not not_189 (not_189_out, OP2);
  not not_190 (not_190_out, OP1);
  not not_191 (not_191_out, OP0);
  not not_192 (not_192_out, F4);
  not not_193 (not_193_out, F3);
  not not_194 (not_194_out, F2);
  not not_195 (not_195_out, F1);
  not not_196 (not_196_out, F0);
  not not_197 (not_197_out, OP5);
  not not_198 (not_198_out, OP4);
  not not_199 (not_199_out, OP3);
  not not_200 (not_200_out, OP2);
  not not_201 (not_201_out, OP1);
  not not_202 (not_202_out, OP0);
  not not_203 (not_203_out, F4);
  not not_204 (not_204_out, F2);
  not not_205 (not_205_out, F0);
  not not_206 (not_206_out, OP5);
  not not_207 (not_207_out, OP4);
  not not_208 (not_208_out, OP2);
  not not_209 (not_209_out, OP1);
  not not_210 (not_210_out, OP0);
  not not_211 (not_211_out, OP4);
  not not_212 (not_212_out, OP3);
  not not_213 (not_213_out, OP2);
  not not_214 (not_214_out, OP5);
  not not_215 (not_215_out, OP4);
  not not_216 (not_216_out, OP1);
  not not_217 (not_217_out, OP0);
  not not_218 (not_218_out, OP5);
  not not_219 (not_219_out, OP4);
  not not_220 (not_220_out, OP3);
  not not_221 (not_221_out, OP2);
  not not_222 (not_222_out, OP1);
  not not_223 (not_223_out, OP0);
  not not_224 (not_224_out, F4);
  not not_225 (not_225_out, F3);
  not not_226 (not_226_out, F1);
  not not_227 (not_227_out, F0);
  not not_228 (not_228_out, OP5);
  not not_229 (not_229_out, OP4);
  not not_230 (not_230_out, OP3);
  not not_231 (not_231_out, OP2);
  not not_232 (not_232_out, OP1);
  not not_233 (not_233_out, OP0);
  not not_234 (not_234_out, F4);
  not not_235 (not_235_out, F3);
  not not_236 (not_236_out, F2);
  not not_237 (not_237_out, F1);
  not not_238 (not_238_out, F0);
  not not_239 (not_239_out, OP5);
  not not_240 (not_240_out, OP4);
  not not_241 (not_241_out, OP3);
  not not_242 (not_242_out, OP2);
  not not_243 (not_243_out, OP1);
  not not_244 (not_244_out, OP0);
  not not_245 (not_245_out, F4);
  not not_246 (not_246_out, F2);
  not not_247 (not_247_out, F0);
  not not_248 (not_248_out, OP5);
  not not_249 (not_249_out, OP4);
  not not_250 (not_250_out, OP3);
  not not_251 (not_251_out, OP2);
  not not_252 (not_252_out, OP1);
  not not_253 (not_253_out, OP0);
  not not_254 (not_254_out, F4);
  not not_255 (not_255_out, F3);
  not not_256 (not_256_out, F1);
  not not_257 (not_257_out, F0);
  and and_1 (Andi, not_1_out, not_2_out, OP3, OP2, not_3_out, not_4_out);
  and and_2 (Halt, not_5_out, not_6_out, not_7_out, not_8_out, not_9_out, not_10_out, not_11_out, not_12_out, F3, F2, not_13_out, not_14_out);
  and and_3 (Jump, not_15_out, not_16_out, not_17_out, not_18_out, OP1, not_19_out);
  and and_4 (MemtoReg, OP5, not_20_out, not_21_out, not_22_out, OP1, OP0);
  and and_5 (Memwrite, OP5, not_23_out, OP3, not_24_out, OP1, OP0);
  and and_6 (Beq, not_25_out, not_26_out, not_27_out, OP2, not_28_out, not_29_out);
  and and_7 (Bne, not_30_out, not_31_out, not_32_out, OP2, not_33_out, OP0);
  and and_8 (and_8_out, not_34_out, not_35_out, not_36_out, not_37_out, not_38_out, not_39_out, F5, not_40_out, F3, not_41_out, F1, not_42_out);
  and and_9 (and_9_out, not_43_out, not_44_out, not_45_out, OP2, not_46_out, not_47_out);
  and and_10 (and_10_out, not_48_out, not_49_out, not_50_out, OP2, not_51_out, OP0);
  and and_11 (and_11_out, not_52_out, not_53_out, not_54_out, not_55_out, not_56_out, not_57_out, F5, not_58_out, not_59_out, not_60_out, not_61_out, not_62_out);
  and and_12 (and_12_out, not_63_out, not_64_out, OP3, not_65_out, not_66_out, not_67_out);
  and and_13 (and_13_out, OP5, not_68_out, not_69_out, not_70_out, OP1, OP0);
  and and_14 (and_14_out, OP5, not_71_out, OP3, not_72_out, OP1, OP0);
  and and_15 (and_15_out, not_73_out, not_74_out, OP3, OP2, not_75_out, not_76_out);
  and and_16 (and_16_out, not_77_out, not_78_out, not_79_out, not_80_out, not_81_out, not_82_out, F5, not_83_out, not_84_out, F2, not_85_out, not_86_out);
  and and_17 (and_17_out, not_87_out, not_88_out, not_89_out, not_90_out, not_91_out, not_92_out, F5, not_93_out, F3, not_94_out, F1, not_95_out);
  and and_18 (and_18_out, not_96_out, not_97_out, not_98_out, OP2, not_99_out, not_100_out);
  and and_19 (and_19_out, not_101_out, not_102_out, not_103_out, OP2, not_104_out, OP0);
  and and_20 (and_20_out, not_105_out, not_106_out, OP3, OP2, not_107_out, not_108_out);
  and and_21 (and_21_out, not_109_out, not_110_out, not_111_out, not_112_out, not_113_out, not_114_out, F5, not_115_out, not_116_out, F2, not_117_out, not_118_out);
  and and_22 (and_22_out, not_119_out, not_120_out, not_121_out, not_122_out, not_123_out, not_124_out, F5, not_125_out, not_126_out, not_127_out, not_128_out, not_129_out);
  and and_23 (and_23_out, not_130_out, not_131_out, not_132_out, not_133_out, not_134_out, not_135_out, F5, not_136_out, F3, not_137_out, F1, not_138_out);
  and and_24 (and_24_out, not_139_out, not_140_out, OP3, not_141_out, not_142_out, not_143_out);
  and and_25 (and_25_out, not_144_out, not_145_out, not_146_out, OP2, not_147_out, not_148_out);
  and and_26 (and_26_out, not_149_out, not_150_out, not_151_out, OP2, not_152_out, OP0);
  and and_27 (and_27_out, OP5, not_153_out, not_154_out, not_155_out, OP1, OP0);
  and and_28 (and_28_out, OP5, not_156_out, OP3, not_157_out, OP1, OP0);
  and and_29 (and_29_out, not_158_out, not_159_out, OP3, OP2, not_160_out, not_161_out);
  and and_30 (and_30_out, not_162_out, not_163_out, not_164_out, not_165_out, not_166_out, not_167_out, F5, not_168_out, not_169_out, F2, not_170_out, not_171_out);
  and and_31 (and_31_out, not_172_out, not_173_out, OP3, not_174_out, not_175_out, not_176_out);
  and and_32 (and_32_out, OP5, not_177_out, not_178_out, not_179_out, OP1, OP0);
  and and_33 (and_33_out, OP5, not_180_out, OP3, not_181_out, OP1, OP0);
  and and_34 (and_34_out, not_182_out, not_183_out, OP3, OP2, not_184_out, not_185_out);
  and and_35 (and_35_out, not_186_out, not_187_out, not_188_out, not_189_out, not_190_out, not_191_out, F5, not_192_out, not_193_out, not_194_out, not_195_out, not_196_out);
  and and_36 (and_36_out, not_197_out, not_198_out, not_199_out, not_200_out, not_201_out, not_202_out, F5, not_203_out, F3, not_204_out, F1, not_205_out);
  and and_37 (and_37_out, not_206_out, not_207_out, OP3, not_208_out, not_209_out, not_210_out);
  and and_38 (and_38_out, OP5, not_211_out, not_212_out, not_213_out, OP1, OP0);
  and and_39 (and_39_out, not_214_out, not_215_out, OP3, OP2, not_216_out, not_217_out);
  and and_40 (and_40_out, not_218_out, not_219_out, not_220_out, not_221_out, not_222_out, not_223_out, F5, not_224_out, not_225_out, F2, not_226_out, not_227_out);
  and and_41 (and_41_out, not_228_out, not_229_out, not_230_out, not_231_out, not_232_out, not_233_out, F5, not_234_out, not_235_out, not_236_out, not_237_out, not_238_out);
  and and_42 (and_42_out, not_239_out, not_240_out, not_241_out, not_242_out, not_243_out, not_244_out, F5, not_245_out, F3, not_246_out, F1, not_247_out);
  and and_43 (and_43_out, not_248_out, not_249_out, not_250_out, not_251_out, not_252_out, not_253_out, F5, not_254_out, not_255_out, F2, not_256_out, not_257_out);
  or or_1 (s3, and_8_out, and_9_out, and_10_out);
  or or_2 (s2, and_11_out, and_12_out, and_13_out, and_14_out, and_15_out, and_16_out);
  or or_3 (s1, and_17_out, and_18_out, and_19_out, and_20_out, and_21_out);
  or or_4 (s0, and_22_out, and_23_out, and_24_out, and_25_out, and_26_out, and_27_out, and_28_out, and_29_out, and_30_out);
  or or_5 (AluSrcB, and_31_out, and_32_out, and_33_out, and_34_out);
  or or_6 (Regwrite, and_35_out, and_36_out, and_37_out, and_38_out, and_39_out, and_40_out);
  or or_7 (RegDst, and_41_out, and_42_out, and_43_out);
endmodule

module \单周期控制器封装  (
  input  [5:0] OP,
  input  [5:0] Funct,
  output Andi,
  output J,
  output Halt,
  output MemtoReg,
  output MemWrite,
  output Beq,
  output [3:0] AluOp,
  output Bne,
  output AluSrcB,
  output RegWrite,
  output RegDst
);

  \单周期万能表格法控制器  \u_单周期万能表格法控制器_1  (
    .OP5(OP[5]), .OP4(OP[4]), .OP3(OP[3]), .OP2(OP[2]), .OP1(OP[1]), .OP0(OP[0]), .F5(Funct[5]),
    .F4(Funct[4]), .F3(Funct[3]), .F2(Funct[2]), .F1(Funct[1]), .F0(Funct[0]), .Andi(Andi), .Halt(Halt),
    .Jump(J), .MemtoReg(MemtoReg), .Memwrite(MemWrite), .Beq(Beq), .Bne(Bne), .s3(AluOp[3]), .s2(AluOp[2]),
    .s1(AluOp[1]), .s0(AluOp[0]), .AluSrcB(AluSrcB), .Regwrite(RegWrite), .RegDst(RegDst));
endmodule

module \多周期MIPS_微程序  (
  output RegWrite,
  output MemWrite,
  output [31:0] PC,
  output [31:0] IR,
  output [31:0] RDin,
  output [31:0] MDin
);

  wire beq_out, bne_out, CLK, comparator_1_lt, mips_alu_1_equal, not_1_out, or_1_out, or_2_out, RST,
       \多周期微程序控制器_1_alusrca , \多周期微程序控制器_1_beq , \多周期微程序控制器_1_bne , \多周期微程序控制器_1_iord ,
       \多周期微程序控制器_1_irwrite , \多周期微程序控制器_1_memread , \多周期微程序控制器_1_memtoreg , \多周期微程序控制器_1_pcsrc ,
       \多周期微程序控制器_1_pcwrite , \多周期微程序控制器_1_regdst ;
  wire [1:0] \多周期微程序控制器_1_alusrcb ;
  wire [3:0] \多周期微程序控制器_1_alu_op , \微地址 ;
  wire [4:0] multiplexer_2_out;
  wire [15:0] \总周期数 ;
  wire [31:0] A_q, bit_extender_1_out, C_q, DR_q, mips_alu_1_result, mips_regifile_1_r1, mips_regifile_1_r2,
       multiplexer_1_out, multiplexer_4_out, multiplexer_5_out, multiplexer_6_out, ram_1_data, shifter_1_out;

  Button \u_总复位  (.out(RST));
  Clock #(.highDuration(1), .lowDuration(1)) clock_1 (.out(CLK));
  // Probe on \微地址 
  // Probe on \总周期数 
  // Probe on \总周期数 
  // Mips_Probe mips_probe_1: pin names not known; wires that end beside it: PC
  Register #(.width(32), .trigger("rising"), .Select("low")) u_PC (
    .D(multiplexer_6_out), .en(or_1_out), .Q(PC), .clk(CLK), .clr(RST));
  Comparator #(.width(4), .mode("unsigned")) comparator_1 (
    .a(\微地址 ), .b(4'b1101), .lt(comparator_1_lt));  // open: gt, eq
  Multiplexer #(.select(1), .width(32), .disabled("Z"), .enable("false")) multiplexer_1 (
    .in0(PC), .in1(C_q), .out(multiplexer_1_out), .sel(\多周期微程序控制器_1_iord ));
  Counter #(.width(16), .max('hffff), .ongoal("wrap"), .trigger("rising"), .behavior("old")) counter_1 (
    .count(comparator_1_lt), .Q(\总周期数 ), .clk(CLK), .clr(RST));  // open: load, D, carry, preset
  // Probe on \微地址 
  RAM #(.addrWidth(10), .dataWidth(32), .bus("separate"), .Select("high")) ram_1 (
    .addr(multiplexer_1_out[11:2]), .din(MDin), .data(ram_1_data), .str(MemWrite), .clk(CLK),
    .ld(\多周期微程序控制器_1_memread ));  // open: sel, clr
  Register #(.width(32), .trigger("rising"), .Select("low")) u_IR (
    .D(ram_1_data), .en(\多周期微程序控制器_1_irwrite ), .Q(IR), .clk(CLK));  // open: clr
  Register #(.width(32), .trigger("rising"), .Select("low")) DR (.D(ram_1_data), .Q(DR_q), .clk(CLK));  // open: en, clr
  Multiplexer #(.select(1), .width(5), .disabled("Z"), .enable("false")) multiplexer_2 (
    .in0(IR[20:16]), .in1(IR[15:11]), .out(multiplexer_2_out), .sel(\多周期微程序控制器_1_regdst ));
  Multiplexer #(.select(1), .width(32), .disabled("Z"), .enable("false")) multiplexer_3 (
    .in0(C_q), .in1(DR_q), .out(RDin), .sel(\多周期微程序控制器_1_memtoreg ));
  assign bit_extender_1_out = {{16{IR[15]}}, IR[15:0]};  // Bit_Extender bit_extender_1
  \多周期微程序控制器  \u_多周期微程序控制器_1  (
    .PcWrite(\多周期微程序控制器_1_pcwrite ), .Beq(\多周期微程序控制器_1_beq ), .PCsrc(\多周期微程序控制器_1_pcsrc ),
    .AluSrcB(\多周期微程序控制器_1_alusrcb ), .AluSrcA(\多周期微程序控制器_1_alusrca ), .RegWrite(RegWrite),
    .MemToReg(\多周期微程序控制器_1_memtoreg ), .RegDst(\多周期微程序控制器_1_regdst ), .IorD(\多周期微程序控制器_1_iord ),
    .MemWrite(MemWrite), .MemRead(\多周期微程序控制器_1_memread ), .IrWrite(\多周期微程序控制器_1_irwrite ),
    .Bne(\多周期微程序控制器_1_bne ), .CLK(CLK), .\当前微指令地址 (\微地址 ), .RST(RST), .OP(IR[31:26]),
    .ALU_OP(\多周期微程序控制器_1_alu_op ), .Func(IR[5:0]));
  MIPS_Regifile mips_regifile_1 (
    .Din(RDin), .Clk(CLK), .R1(mips_regifile_1_r1), .R2(mips_regifile_1_r2), .WE(RegWrite),
    .W_num(multiplexer_2_out), .R1_num(IR[25:21]), .R2_num(IR[20:16]));
  Register #(.width(32), .trigger("rising"), .Select("low")) B (
    .D(mips_regifile_1_r2), .Q(MDin), .clk(CLK));  // open: en, clr
  Multiplexer #(.select(1), .width(32), .disabled("Z"), .enable("false")) multiplexer_4 (
    .in0(PC), .in1(A_q), .out(multiplexer_4_out), .sel(\多周期微程序控制器_1_alusrca ));
  Register #(.width(32), .trigger("rising"), .Select("low")) A (
    .D(mips_regifile_1_r1), .Q(A_q), .clk(CLK));  // open: en, clr
  Shifter #(.width(32), .shift("ll")) shifter_1 (.in(bit_extender_1_out), .\dist (5'b00010), .out(shifter_1_out));
  Multiplexer #(.select(2), .width(32), .disabled("Z"), .enable("false")) multiplexer_5 (
    .in0(MDin), .in1(32'h4), .in2(bit_extender_1_out), .in3(shifter_1_out), .out(multiplexer_5_out),
    .sel(\多周期微程序控制器_1_alusrcb ));
  MIPS_ALU mips_alu_1 (
    .X(multiplexer_4_out), .Y(multiplexer_5_out), .AluOP(\多周期微程序控制器_1_alu_op ), .Equal(mips_alu_1_equal),
    .Result(mips_alu_1_result));  // open: Result_2
  not not_1 (not_1_out, mips_alu_1_equal);
  Register #(.width(32), .trigger("rising"), .Select("low")) C (
    .D(mips_alu_1_result), .Q(C_q), .clk(CLK));  // open: en, clr
  and beq (beq_out, mips_alu_1_equal, \多周期微程序控制器_1_beq );
  and bne (bne_out, not_1_out, \多周期微程序控制器_1_bne );
  or or_1 (or_1_out, \多周期微程序控制器_1_pcwrite , or_2_out);
  or or_2 (or_2_out, beq_out, bne_out);
  Multiplexer #(.select(1), .width(32), .disabled("Z"), .enable("false")) multiplexer_6 (
    .in0(mips_alu_1_result), .in1(C_q), .out(multiplexer_6_out), .sel(\多周期微程序控制器_1_pcsrc ));

  // Notes on the sheet:
  //   加载sort.hex，程序执行会停机并进行内存排序
  //   参考值：891
  //   为方便自动评测，需要输出PC，IR，寄存器文件写入端口RDin，内存写入端口MDin等信号
  //   存储器
  //   IorD
  //   MemWrite
  //   MemRead
  //   IRWrite
  //   OP
  //   Func
  //   RegDst
  //   PcWrite
  //   Beq
  //   Bne
  //   PcSrc
  //   AluOP
  //   AluSrcB
  //   AluSrcA
  //   RegWrite
  //   MemToReg
endmodule

// 微程序控制器
module \多周期微程序控制器  (
  input  [5:0] OP,
  input  [5:0] Func,
  input  CLK,
  input  RST,
  output [3:0] ALU_OP,
  output Bne,
  output Beq,
  output MemRead,
  output MemWrite,
  output RegWrite,
  output PcWrite,
  output IrWrite,
  output RegDst,
  output MemToReg,
  output [3:0] \当前微指令地址 ,
  output [1:0] AluSrcB,
  output AluSrcA,
  output PCsrc,
  output IorD
);

  wire ADD, ADDI, BEQ_t, BNE_t, comparator_6_eq, comparator_7_eq, comparator_8_eq, comparator_9_eq, I_Type,
       LW, P, R_TYPE, SLT, SW, SysCall;
  wire [1:0] ALU_Control;
  wire [3:0] controlled_buffer_1_out, multiplexer_1_out, rom_1_data, \微程序地址转移逻辑_1_s0 ;

  Comparator #(.width(6), .mode("twosComplement")) comparator_1 (.a(OP), .b(6'b100011), .eq(LW));  // open: gt, lt
  Comparator #(.width(6), .mode("twosComplement")) comparator_2 (.a(OP), .b(6'b101011), .eq(SW));  // open: gt, lt
  Comparator #(.width(6), .mode("twosComplement")) comparator_3 (.a(OP), .b(6'b000100), .eq(BEQ_t));  // open: gt, lt
  Comparator #(.width(6), .mode("twosComplement")) comparator_4 (.a(OP), .b(6'b000101), .eq(BNE_t));  // open: gt, lt
  Comparator #(.width(6), .mode("twosComplement")) comparator_5 (.a(OP), .b(6'b001000), .eq(ADDI));  // open: gt, lt
  Comparator #(.width(6), .mode("twosComplement")) comparator_6 (
    .a(OP), .b({6{1'b0}}), .eq(comparator_6_eq));  // open: gt, lt
  \微程序地址转移逻辑  \u_微程序地址转移逻辑_1  (
    .R_Type(R_TYPE), .S3(\微程序地址转移逻辑_1_s0 [3]), .ADDI(ADDI), .S2(\微程序地址转移逻辑_1_s0 [2]), .LW(LW),
    .S1(\微程序地址转移逻辑_1_s0 [1]), .SW(SW), .S0(\微程序地址转移逻辑_1_s0 [0]), .BEQ(BEQ_t), .BNE(BNE_t), .SYSCALL(SysCall));
  Comparator #(.width(6), .mode("twosComplement")) comparator_7 (
    .a(Func), .b(6'b100000), .eq(comparator_7_eq));  // open: gt, lt
  Comparator #(.width(6), .mode("twosComplement")) comparator_8 (
    .a(Func), .b(6'b101010), .eq(comparator_8_eq));  // open: gt, lt
  Comparator #(.width(6), .mode("twosComplement")) comparator_9 (
    .a(Func), .b(6'b001100), .eq(comparator_9_eq));  // open: gt, lt
  or or_1 (R_TYPE, ADD, SLT);
  and and_1 (ADD, comparator_7_eq, comparator_6_eq);
  and and_2 (SLT, comparator_8_eq, comparator_6_eq);
  and and_3 (SysCall, comparator_9_eq, comparator_6_eq);
  Register #(.width(4), .trigger("rising"), .Select("low")) register_1 (
    .D(multiplexer_1_out), .Q(\当前微指令地址 ), .clk(CLK), .clr(RST));  // open: en
  Multiplexer #(.select(1), .width(4), .disabled("Z"), .enable("false")) multiplexer_1 (
    .in0(rom_1_data), .in1(\微程序地址转移逻辑_1_s0 ), .out(multiplexer_1_out), .sel(P));
  or or_2 (I_Type, ADDI, LW, SW, BEQ_t, BNE_t);
  assign controlled_buffer_1_out = SLT ? 4'b1011 : 4'bz;  // Controlled_Buffer controlled_buffer_1
  ROM #(.addrWidth(4), .dataWidth(21), .Select("high")) rom_1 (
    .addr(\当前微指令地址 ),
    .data({IorD, PCsrc, AluSrcA, AluSrcB, MemToReg, RegDst, IrWrite, PcWrite, RegWrite, MemWrite, MemRead, Beq, Bne, ALU_Control, P, rom_1_data}));
  assign controlled_buffer_1_out = ADDI ? 4'b0101 : 4'bz;  // Controlled_Buffer controlled_buffer_2
  assign controlled_buffer_1_out = ADD ? 4'b0101 : 4'bz;  // Controlled_Buffer controlled_buffer_3
  Multiplexer #(.select(2), .width(4), .disabled("Z"), .enable("false")) multiplexer_2 (
    .in0(4'b0101), .in1(4'b0110), .in2(controlled_buffer_1_out), .out(ALU_OP), .sel(ALU_Control));  // open: in3

  // Notes on the sheet:
  //   指令译码信号
  //   根据指令进行微程序地址转移
  //   指令译码逻辑
  //   给出简单的逻辑实现对应指令译码信号，LW、SW、BEQ、BNE、ADDI、ADD、SLT、SYSCALL、R_TYPE。
  //   下址字段
  //   微程序
  //   入口地址
  //   判断逻辑
  //   μAR
  //   控制存储器
  //   contents of rom_1 (hex, n*v repeats v):
  //   13201 30010 60003 100204 8800 60006 100400 40048 4800 c0140 c00c0 6004c 800 d
  //   微命令
  //   ALU控制器逻辑
  //   注意R_TYPE表示R型运算指令，SYSCALL是特殊的R型指令，不属于这个类别
  //   微指令
  //   根据ALU_Control的值决定运算器运算选择控制信号ALU_OP的值
  //   下址字段
  //   判断逻辑
  //   ALU_Control= 00 运算器做加法
  //   ALU_Control= 01 运算器做减法
  //   ALU_Control= 10 运算方式由Func决定 
endmodule

// 地址转移逻辑
module \微程序地址转移逻辑  (
  input  R_Type,
  input  ADDI,
  input  LW,
  input  SW,
  input  BEQ,
  input  BNE,
  input  SYSCALL,
  output S3,
  output S2,
  output S1,
  output S0
);

  or or_1 (S3, SYSCALL, BNE, BEQ, ADDI);
  or or_2 (S2, SYSCALL, SW, R_Type);
  or or_3 (S1, BNE, LW, ADDI, R_Type);
  or or_4 (S0, SYSCALL, BEQ, SW, ADDI, R_Type);
endmodule

module \多周期MIPS_硬布线  (
  output RegWrite,
  output MemWrite,
  output [31:0] PC,
  output [31:0] IR,
  output [31:0] RDin,
  output [31:0] MDin
);

  wire and_1_out, and_2_out, CLK, comparator_1_lt, mips_alu_1_equal, not_1_out, or_1_out, or_2_out, RST,
       \多周期硬布线控制器_1_alusrca , \多周期硬布线控制器_1_beq , \多周期硬布线控制器_1_bne , \多周期硬布线控制器_1_iord ,
       \多周期硬布线控制器_1_irwrite , \多周期硬布线控制器_1_memread , \多周期硬布线控制器_1_memtoreg , \多周期硬布线控制器_1_pcsrc ,
       \多周期硬布线控制器_1_pcwrite , \多周期硬布线控制器_1_regdst ;
  wire [1:0] \多周期硬布线控制器_1_alusrcb ;
  wire [3:0] \多周期硬布线控制器_1_alu_op , \现态 ;
  wire [4:0] multiplexer_2_out;
  wire [15:0] \总周期数 ;
  wire [31:0] A_q, bit_extender_1_out, C_q, DR_q, mips_alu_1_result, mips_regifile_1_r1, mips_regifile_1_r2,
       multiplexer_1_out, multiplexer_4_out, multiplexer_5_out, multiplexer_6_out, ram_1_data, shifter_1_out;

  Button \u_总复位  (.out(RST));
  Clock #(.highDuration(1), .lowDuration(1)) clock_1 (.out(CLK));
  Register #(.width(32), .trigger("rising"), .Select("low")) u_PC (
    .D(multiplexer_6_out), .en(or_1_out), .Q(PC), .clk(CLK), .clr(RST));
  // Probe on \现态 
  Counter #(.width(16), .max('hffff), .ongoal("wrap"), .trigger("rising"), .behavior("old")) counter_1 (
    .count(comparator_1_lt), .Q(\总周期数 ), .clk(CLK), .clr(RST));  // open: load, D, carry, preset
  Comparator #(.width(4), .mode("unsigned")) comparator_1 (
    .a(\现态 ), .b(4'b1101), .lt(comparator_1_lt));  // open: gt, eq
  // Probe on \总周期数 
  // Probe on \总周期数 
  Multiplexer #(.select(1), .width(32), .disabled("Z"), .enable("false")) multiplexer_1 (
    .in0(PC), .in1(C_q), .out(multiplexer_1_out), .sel(\多周期硬布线控制器_1_iord ));
  // Probe on \现态 
  RAM #(.addrWidth(10), .dataWidth(32), .bus("separate"), .Select("high")) ram_1 (
    .addr(multiplexer_1_out[11:2]), .din(MDin), .data(ram_1_data), .str(MemWrite), .clk(CLK),
    .ld(\多周期硬布线控制器_1_memread ));  // open: sel, clr
  Register #(.width(32), .trigger("rising"), .Select("low")) u_IR (
    .D(ram_1_data), .en(\多周期硬布线控制器_1_irwrite ), .Q(IR), .clk(CLK));  // open: clr
  Register #(.width(32), .trigger("rising"), .Select("low")) DR (.D(ram_1_data), .Q(DR_q), .clk(CLK));  // open: en, clr
  Multiplexer #(.select(1), .width(5), .disabled("Z"), .enable("false")) multiplexer_2 (
    .in0(IR[20:16]), .in1(IR[15:11]), .out(multiplexer_2_out), .sel(\多周期硬布线控制器_1_regdst ));
  Multiplexer #(.select(1), .width(32), .disabled("Z"), .enable("false")) multiplexer_3 (
    .in0(C_q), .in1(DR_q), .out(RDin), .sel(\多周期硬布线控制器_1_memtoreg ));
  \多周期硬布线控制器  \u_多周期硬布线控制器_1  (
    .RST(RST), .AluSrcB(\多周期硬布线控制器_1_alusrcb ), .OP(IR[31:26]), .CLK(CLK), .\当前状态 (\现态 ),
    .IorD(\多周期硬布线控制器_1_iord ), .PCsrc(\多周期硬布线控制器_1_pcsrc ), .AluSrcA(\多周期硬布线控制器_1_alusrca ),
    .MemToReg(\多周期硬布线控制器_1_memtoreg ), .RegDst(\多周期硬布线控制器_1_regdst ), .IrWrite(\多周期硬布线控制器_1_irwrite ),
    .PcWrite(\多周期硬布线控制器_1_pcwrite ), .RegWrite(RegWrite), .MemWrite(MemWrite),
    .MemRead(\多周期硬布线控制器_1_memread ), .Beq(\多周期硬布线控制器_1_beq ), .Bne(\多周期硬布线控制器_1_bne ), .Func(IR[5:0]),
    .ALU_OP(\多周期硬布线控制器_1_alu_op ));
  assign bit_extender_1_out = {{16{IR[15]}}, IR[15:0]};  // Bit_Extender bit_extender_1
  MIPS_Regifile mips_regifile_1 (
    .Din(RDin), .Clk(CLK), .R1(mips_regifile_1_r1), .R2(mips_regifile_1_r2), .WE(RegWrite),
    .W_num(multiplexer_2_out), .R1_num(IR[25:21]), .R2_num(IR[20:16]));
  Register #(.width(32), .trigger("rising"), .Select("low")) B (
    .D(mips_regifile_1_r2), .Q(MDin), .clk(CLK));  // open: en, clr
  Multiplexer #(.select(1), .width(32), .disabled("Z"), .enable("false")) multiplexer_4 (
    .in0(PC), .in1(A_q), .out(multiplexer_4_out), .sel(\多周期硬布线控制器_1_alusrca ));
  Register #(.width(32), .trigger("rising"), .Select("low")) A (
    .D(mips_regifile_1_r1), .Q(A_q), .clk(CLK));  // open: en, clr
  Shifter #(.width(32), .shift("ll")) shifter_1 (.in(bit_extender_1_out), .\dist (5'b00010), .out(shifter_1_out));
  Multiplexer #(.select(2), .width(32), .disabled("Z"), .enable("false")) multiplexer_5 (
    .in0(MDin), .in1(32'h4), .in2(bit_extender_1_out), .in3(shifter_1_out), .out(multiplexer_5_out),
    .sel(\多周期硬布线控制器_1_alusrcb ));
  MIPS_ALU mips_alu_1 (
    .X(multiplexer_4_out), .Y(multiplexer_5_out), .AluOP(\多周期硬布线控制器_1_alu_op ), .Equal(mips_alu_1_equal),
    .Result(mips_alu_1_result));  // open: Result_2
  Register #(.width(32), .trigger("rising"), .Select("low")) C (
    .D(mips_alu_1_result), .Q(C_q), .clk(CLK));  // open: en, clr
  and and_1 (and_1_out, mips_alu_1_equal, \多周期硬布线控制器_1_beq );
  not not_1 (not_1_out, mips_alu_1_equal);
  and and_2 (and_2_out, not_1_out, \多周期硬布线控制器_1_bne );
  Multiplexer #(.select(1), .width(32), .disabled("Z"), .enable("false")) multiplexer_6 (
    .in0(mips_alu_1_result), .in1(C_q), .out(multiplexer_6_out), .sel(\多周期硬布线控制器_1_pcsrc ));
  or or_1 (or_1_out, \多周期硬布线控制器_1_pcwrite , or_2_out);
  or or_2 (or_2_out, and_1_out, and_2_out);

  // Notes on the sheet:
  //   加载sort.hex，程序执行会停机并进行内存排序
  //   参考值：891
  //   存储器
  //   为方便自动评测，需要输出PC，IR，寄存器文件写入端口RDin，内存写入端口MDin等信号
  //   IorD
  //   MemWrite
  //   MemRead
  //   IRWrite
  //   OP
  //   Func
  //   RegDst
  //   Beq
  //   Bne
  //   PcWrite
  //   PcSrc
  //   AluOP
  //   AluSrcB
  //   AluSrcA
  //   RegWrite
  //   MemToReg
endmodule

// 硬布线控制器
module \多周期硬布线控制器  (
  input  [5:0] OP,
  input  [5:0] Func,
  input  CLK,
  input  RST,
  output [3:0] ALU_OP,
  output Bne,
  output Beq,
  output MemRead,
  output MemWrite,
  output RegWrite,
  output PcWrite,
  output IrWrite,
  output RegDst,
  output MemToReg,
  output [3:0] \当前状态 ,
  output [1:0] AluSrcB,
  output AluSrcA,
  output PCsrc,
  output IorD
);

  wire ADD, ADDI, AND, ANDI, BEQ_t, BNE_t, comparator_6_eq, comparator_9_eq, comparator_10_eq,
       comparator_11_eq, comparator_12_eq, I_TYPE, J, LW, or_3_out, or_4_out, P, R_TYPE, SLT, SW, SysCall;
  wire [1:0] ALU_Control;
  wire [3:0] controlled_buffer_1_out, fsm_1_n0, rom_1_data;

  Comparator #(.width(6), .mode("twosComplement")) comparator_1 (.a(OP), .b(6'b100011), .eq(LW));  // open: gt, lt
  Comparator #(.width(6), .mode("twosComplement")) comparator_2 (.a(OP), .b(6'b101011), .eq(SW));  // open: gt, lt
  Comparator #(.width(6), .mode("twosComplement")) comparator_3 (.a(OP), .b(6'b000100), .eq(BEQ_t));  // open: gt, lt
  Comparator #(.width(6), .mode("twosComplement")) comparator_4 (.a(OP), .b(6'b000101), .eq(BNE_t));  // open: gt, lt
  Comparator #(.width(6), .mode("twosComplement")) comparator_5 (.a(OP), .b(6'b001000), .eq(ADDI));  // open: gt, lt
  Comparator #(.width(6), .mode("twosComplement")) comparator_6 (
    .a(OP), .b({6{1'b0}}), .eq(comparator_6_eq));  // open: gt, lt
  Comparator #(.width(6), .mode("twosComplement")) comparator_7 (.a(OP), .b(6'b000010), .eq(J));  // open: gt, lt
  Comparator #(.width(6), .mode("twosComplement")) comparator_8 (.a(OP), .b(6'b001100), .eq(ANDI));  // open: gt, lt
  FSM fsm_1 (
    .S3(\当前状态 [3]), .S2(\当前状态 [2]), .S1(\当前状态 [1]), .S0(\当前状态 [0]), .R_Type(R_TYPE), .I_Type(I_TYPE),
    .LW(LW), .SW(SW), .BEQ(BEQ_t), .BNE(BNE_t), .SYSCALL(SysCall), .J(J), .N3(fsm_1_n0[3]), .N2(fsm_1_n0[2]),
    .N1(fsm_1_n0[1]), .N0(fsm_1_n0[0]));
  Comparator #(.width(6), .mode("twosComplement")) comparator_9 (
    .a(Func), .b(6'b100000), .eq(comparator_9_eq));  // open: gt, lt
  Comparator #(.width(6), .mode("twosComplement")) comparator_10 (
    .a(Func), .b(6'b101010), .eq(comparator_10_eq));  // open: gt, lt
  Comparator #(.width(6), .mode("twosComplement")) comparator_11 (
    .a(Func), .b(6'b001100), .eq(comparator_11_eq));  // open: gt, lt
  Comparator #(.width(6), .mode("twosComplement")) comparator_12 (
    .a(Func), .b(6'b100100), .eq(comparator_12_eq));  // open: gt, lt
  or or_1 (R_TYPE, ADD, SLT);
  and and_1 (ADD, comparator_9_eq, comparator_6_eq);
  and and_2 (SLT, comparator_10_eq, comparator_6_eq);
  and and_3 (SysCall, comparator_11_eq, comparator_6_eq);
  and and_4 (AND, comparator_12_eq, comparator_6_eq);
  or or_2 (I_TYPE, ANDI, ADDI);
  Register #(.width(4), .trigger("rising"), .Select("low")) register_1 (
    .D(fsm_1_n0), .Q(\当前状态 ), .clk(CLK), .clr(RST));  // open: en
  ROM #(.addrWidth(4), .dataWidth(21), .Select("high")) rom_1 (
    .addr(\当前状态 ),
    .data({IorD, PCsrc, AluSrcA, AluSrcB, MemToReg, RegDst, IrWrite, PcWrite, RegWrite, MemWrite, MemRead, Beq, Bne, ALU_Control, P, rom_1_data}));
  assign controlled_buffer_1_out = or_3_out ? 4'b0101 : 4'bz;  // Controlled_Buffer controlled_buffer_1
  or or_3 (or_3_out, ADDI, ADD);
  assign controlled_buffer_1_out = or_4_out ? 4'b0111 : 4'bz;  // Controlled_Buffer controlled_buffer_2
  or or_4 (or_4_out, AND, ANDI);
  assign controlled_buffer_1_out = SLT ? 4'b1011 : 4'bz;  // Controlled_Buffer controlled_buffer_3
  assign controlled_buffer_1_out = J ? 4'b1000 : 4'bz;  // Controlled_Buffer controlled_buffer_4
  Multiplexer #(.select(2), .width(4), .disabled("Z"), .enable("false")) multiplexer_1 (
    .in0(4'b0101), .in1(4'b0110), .in2(controlled_buffer_1_out), .out(ALU_OP), .sel(ALU_Control));  // open: in3

  // Notes on the sheet:
  //   指令译码信号
  //   现态
  //   组合逻辑
  //   指令译码逻辑
  //   次态
  //   状态寄存器
  //   控制存储器
  //   contents of rom_1 (hex, n*v repeats v):
  //   13201 30010 60003 100204 8800 60006 100400 40048 4800 c0140 c00c0 6004c 800 d 0 e1040
  //   ALU控制器逻辑
  //   根据ALU_Control的值决定运算器运算选择控制信号ALU_OP的值
  //   ALU_Control= 00 运算器做加法
  //   ALU_Control= 01 运算器做减法
  //   ALU_Control= 10 运算方式由Func决定 
endmodule

module FSM (
  input  S3,
  input  S2,
  input  S1,
  input  S0,
  input  R_Type,
  input  I_Type,
  input  LW,
  input  SW,
  input  BEQ,
  input  BNE,
  input  SYSCALL,
  input  J,
  output N3,
  output N2,
  output N1,
  output N0
);

  wire and_1_out, and_2_out, and_3_out, and_4_out, and_5_out, and_6_out, and_7_out, and_8_out, and_9_out,
       and_10_out, and_11_out, and_12_out, and_13_out, and_14_out, and_15_out, and_16_out, and_17_out,
       and_18_out, and_19_out, and_20_out, and_21_out, and_22_out, and_23_out, and_24_out, and_25_out,
       and_26_out, and_27_out, and_28_out, and_29_out, and_30_out, and_31_out, and_32_out, not_1_out,
       not_2_out, not_3_out, not_4_out, not_5_out, not_6_out, not_7_out, not_8_out, not_9_out, not_10_out,
       not_11_out, not_12_out, not_13_out, not_14_out, not_15_out, not_16_out, not_17_out, not_18_out,
       not_19_out, not_20_out, not_21_out, not_22_out, not_23_out, not_24_out, not_25_out, not_26_out,
       not_27_out, not_28_out, not_29_out, not_30_out, not_31_out, not_32_out, not_33_out, not_34_out,
       not_35_out, not_36_out, not_37_out, not_38_out, not_39_out, not_40_out, not_41_out, not_42_out,
       not_43_out, not_44_out, not_45_out, not_46_out, not_47_out, not_48_out, not_49_out, not_50_out,
       not_51_out, not_52_out, not_53_out, not_54_out, not_55_out, not_56_out, not_57_out, not_58_out,
       not_59_out, not_60_out, not_61_out, not_62_out, not_63_out, not_64_out, not_65_out, not_66_out,
       not_67_out, not_68_out, not_69_out, not_70_out, not_71_out, not_72_out, not_73_out, not_74_out,
       not_75_out, not_76_out, not_77_out, not_78_out, not_79_out, not_80_out, not_81_out, not_82_out,
       not_83_out, not_84_out, not_85_out, not_86_out, not_87_out, not_88_out, not_89_out, not_90_out,
       not_91_out, not_92_out, not_93_out, not_94_out, not_95_out, not_96_out, not_97_out, not_98_out,
       not_99_out, not_100_out, not_101_out, not_102_out, not_103_out, not_104_out, not_105_out, not_106_out,
       not_107_out, not_108_out, not_109_out, not_110_out, not_111_out, not_112_out, not_113_out,
       not_114_out, not_115_out, not_116_out, not_117_out, not_118_out, not_119_out, not_120_out,
       not_121_out, not_122_out, not_123_out, not_124_out, not_125_out, not_126_out, not_127_out,
       not_128_out, not_129_out, not_130_out, not_131_out, not_132_out, not_133_out, not_134_out,
       not_135_out, not_136_out, not_137_out, not_138_out, not_139_out, not_140_out, not_141_out,
       not_142_out, not_143_out, not_144_out, not_145_out, not_146_out, not_147_out, not_148_out,
       not_149_out, not_150_out, not_151_out, not_152_out, not_153_out, not_154_out, not_155_out,
       not_156_out, not_157_out, not_158_out, not_159_out, not_160_out, not_161_out, not_162_out,
       not_163_out, not_164_out, not_165_out, not_166_out, not_167_out, not_168_out, not_169_out,
       not_170_out, not_171_out, not_172_out, not_173_out, not_174_out, not_175_out, not_176_out,
       not_177_out, not_178_out, not_179_out, not_180_out, not_181_out, not_182_out, not_183_out,
       not_184_out, not_185_out, not_186_out, not_187_out, not_188_out, not_189_out, not_190_out,
       not_191_out, not_192_out, not_193_out, not_194_out, not_195_out, not_196_out, not_197_out,
       not_198_out, not_199_out, not_200_out, not_201_out, not_202_out, not_203_out, not_204_out,
       not_205_out, not_206_out;

  not not_1 (not_1_out, S3);
  not not_2 (not_2_out, S2);
  not not_3 (not_3_out, S1);
  not not_4 (not_4_out, R_Type);
  not not_5 (not_5_out, LW);
  not not_6 (not_6_out, SW);
  not not_7 (not_7_out, BEQ);
  not not_8 (not_8_out, BNE);
  not not_9 (not_9_out, SYSCALL);
  not not_10 (not_10_out, J);
  not not_11 (not_11_out, S3);
  not not_12 (not_12_out, S2);
  not not_13 (not_13_out, S1);
  not not_14 (not_14_out, R_Type);
  not not_15 (not_15_out, I_Type);
  not not_16 (not_16_out, LW);
  not not_17 (not_17_out, SW);
  not not_18 (not_18_out, BNE);
  not not_19 (not_19_out, SYSCALL);
  not not_20 (not_20_out, J);
  not not_21 (not_21_out, S3);
  not not_22 (not_22_out, S2);
  not not_23 (not_23_out, S1);
  not not_24 (not_24_out, R_Type);
  not not_25 (not_25_out, I_Type);
  not not_26 (not_26_out, LW);
  not not_27 (not_27_out, SW);
  not not_28 (not_28_out, BEQ);
  not not_29 (not_29_out, SYSCALL);
  not not_30 (not_30_out, J);
  not not_31 (not_31_out, S3);
  not not_32 (not_32_out, S2);
  not not_33 (not_33_out, S1);
  not not_34 (not_34_out, R_Type);
  not not_35 (not_35_out, I_Type);
  not not_36 (not_36_out, LW);
  not not_37 (not_37_out, SW);
  not not_38 (not_38_out, BEQ);
  not not_39 (not_39_out, BNE);
  not not_40 (not_40_out, J);
  not not_41 (not_41_out, S3);
  not not_42 (not_42_out, S2);
  not not_43 (not_43_out, S1);
  not not_44 (not_44_out, S3);
  not not_45 (not_45_out, S2);
  not not_46 (not_46_out, S1);
  not not_47 (not_47_out, R_Type);
  not not_48 (not_48_out, I_Type);
  not not_49 (not_49_out, SYSCALL);
  not not_50 (not_50_out, S3);
  not not_51 (not_51_out, S2);
  not not_52 (not_52_out, S1);
  not not_53 (not_53_out, I_Type);
  not not_54 (not_54_out, LW);
  not not_55 (not_55_out, SW);
  not not_56 (not_56_out, BEQ);
  not not_57 (not_57_out, BNE);
  not not_58 (not_58_out, SYSCALL);
  not not_59 (not_59_out, J);
  not not_60 (not_60_out, S3);
  not not_61 (not_61_out, S2);
  not not_62 (not_62_out, S1);
  not not_63 (not_63_out, R_Type);
  not not_64 (not_64_out, I_Type);
  not not_65 (not_65_out, LW);
  not not_66 (not_66_out, BEQ);
  not not_67 (not_67_out, BNE);
  not not_68 (not_68_out, SYSCALL);
  not not_69 (not_69_out, J);
  not not_70 (not_70_out, S3);
  not not_71 (not_71_out, S2);
  not not_72 (not_72_out, S1);
  not not_73 (not_73_out, R_Type);
  not not_74 (not_74_out, I_Type);
  not not_75 (not_75_out, LW);
  not not_76 (not_76_out, SW);
  not not_77 (not_77_out, BEQ);
  not not_78 (not_78_out, BNE);
  not not_79 (not_79_out, J);
  not not_80 (not_80_out, S3);
  not not_81 (not_81_out, S2);
  not not_82 (not_82_out, S3);
  not not_83 (not_83_out, S1);
  not not_84 (not_84_out, S2);
  not not_85 (not_85_out, S1);
  not not_86 (not_86_out, S3);
  not not_87 (not_87_out, S2);
  not not_88 (not_88_out, S1);
  not not_89 (not_89_out, R_Type);
  not not_90 (not_90_out, I_Type);
  not not_91 (not_91_out, SYSCALL);
  not not_92 (not_92_out, S3);
  not not_93 (not_93_out, S2);
  not not_94 (not_94_out, S1);
  not not_95 (not_95_out, I_Type);
  not not_96 (not_96_out, LW);
  not not_97 (not_97_out, SW);
  not not_98 (not_98_out, BEQ);
  not not_99 (not_99_out, BNE);
  not not_100 (not_100_out, SYSCALL);
  not not_101 (not_101_out, J);
  not not_102 (not_102_out, S3);
  not not_103 (not_103_out, S2);
  not not_104 (not_104_out, S1);
  not not_105 (not_105_out, R_Type);
  not not_106 (not_106_out, LW);
  not not_107 (not_107_out, SW);
  not not_108 (not_108_out, BEQ);
  not not_109 (not_109_out, BNE);
  not not_110 (not_110_out, SYSCALL);
  not not_111 (not_111_out, J);
  not not_112 (not_112_out, S3);
  not not_113 (not_113_out, S2);
  not not_114 (not_114_out, S1);
  not not_115 (not_115_out, R_Type);
  not not_116 (not_116_out, I_Type);
  not not_117 (not_117_out, SW);
  not not_118 (not_118_out, BEQ);
  not not_119 (not_119_out, BNE);
  not not_120 (not_120_out, SYSCALL);
  not not_121 (not_121_out, J);
  not not_122 (not_122_out, S3);
  not not_123 (not_123_out, S2);
  not not_124 (not_124_out, S1);
  not not_125 (not_125_out, R_Type);
  not not_126 (not_126_out, I_Type);
  not not_127 (not_127_out, LW);
  not not_128 (not_128_out, SW);
  not not_129 (not_129_out, BEQ);
  not not_130 (not_130_out, SYSCALL);
  not not_131 (not_131_out, J);
  not not_132 (not_132_out, S3);
  not not_133 (not_133_out, S2);
  not not_134 (not_134_out, S0);
  not not_135 (not_135_out, S3);
  not not_136 (not_136_out, S1);
  not not_137 (not_137_out, S3);
  not not_138 (not_138_out, S2);
  not not_139 (not_139_out, S1);
  not not_140 (not_140_out, R_Type);
  not not_141 (not_141_out, I_Type);
  not not_142 (not_142_out, SYSCALL);
  not not_143 (not_143_out, S3);
  not not_144 (not_144_out, S2);
  not not_145 (not_145_out, S1);
  not not_146 (not_146_out, S0);
  not not_147 (not_147_out, S3);
  not not_148 (not_148_out, S2);
  not not_149 (not_149_out, S1);
  not not_150 (not_150_out, I_Type);
  not not_151 (not_151_out, LW);
  not not_152 (not_152_out, SW);
  not not_153 (not_153_out, BEQ);
  not not_154 (not_154_out, BNE);
  not not_155 (not_155_out, SYSCALL);
  not not_156 (not_156_out, J);
  not not_157 (not_157_out, S3);
  not not_158 (not_158_out, S2);
  not not_159 (not_159_out, S1);
  not not_160 (not_160_out, R_Type);
  not not_161 (not_161_out, LW);
  not not_162 (not_162_out, SW);
  not not_163 (not_163_out, BEQ);
  not not_164 (not_164_out, BNE);
  not not_165 (not_165_out, SYSCALL);
  not not_166 (not_166_out, J);
  not not_167 (not_167_out, S3);
  not not_168 (not_168_out, S2);
  not not_169 (not_169_out, S1);
  not not_170 (not_170_out, R_Type);
  not not_171 (not_171_out, I_Type);
  not not_172 (not_172_out, LW);
  not not_173 (not_173_out, BEQ);
  not not_174 (not_174_out, BNE);
  not not_175 (not_175_out, SYSCALL);
  not not_176 (not_176_out, J);
  not not_177 (not_177_out, S3);
  not not_178 (not_178_out, S2);
  not not_179 (not_179_out, S1);
  not not_180 (not_180_out, R_Type);
  not not_181 (not_181_out, I_Type);
  not not_182 (not_182_out, LW);
  not not_183 (not_183_out, SW);
  not not_184 (not_184_out, BNE);
  not not_185 (not_185_out, SYSCALL);
  not not_186 (not_186_out, J);
  not not_187 (not_187_out, S3);
  not not_188 (not_188_out, S2);
  not not_189 (not_189_out, S1);
  not not_190 (not_190_out, R_Type);
  not not_191 (not_191_out, I_Type);
  not not_192 (not_192_out, LW);
  not not_193 (not_193_out, SW);
  not not_194 (not_194_out, BEQ);
  not not_195 (not_195_out, BNE);
  not not_196 (not_196_out, J);
  not not_197 (not_197_out, S3);
  not not_198 (not_198_out, S2);
  not not_199 (not_199_out, S0);
  not not_200 (not_200_out, S1);
  not not_201 (not_201_out, S3);
  not not_202 (not_202_out, S2);
  not not_203 (not_203_out, S1);
  not not_204 (not_204_out, R_Type);
  not not_205 (not_205_out, I_Type);
  not not_206 (not_206_out, SYSCALL);
  and and_1 (and_1_out, not_1_out, not_2_out, not_3_out, S0, not_4_out, I_Type, not_5_out, not_6_out, not_7_out, not_8_out, not_9_out, not_10_out);
  and and_2 (and_2_out, not_11_out, not_12_out, not_13_out, S0, not_14_out, not_15_out, not_16_out, not_17_out, BEQ, not_18_out, not_19_out, not_20_out);
  and and_3 (and_3_out, not_21_out, not_22_out, not_23_out, S0, not_24_out, not_25_out, not_26_out, not_27_out, not_28_out, BNE, not_29_out, not_30_out);
  and and_4 (and_4_out, not_31_out, not_32_out, not_33_out, S0, not_34_out, not_35_out, not_36_out, not_37_out, not_38_out, not_39_out, SYSCALL, not_40_out);
  and and_5 (and_5_out, not_41_out, S2, S1, S0);
  and and_6 (and_6_out, S3, not_42_out, S1, S0);
  and and_7 (and_7_out, S3, S2, not_43_out, S0);
  and and_8 (and_8_out, not_44_out, not_45_out, not_46_out, S0, not_47_out, not_48_out, not_49_out, J);
  and and_9 (and_9_out, not_50_out, not_51_out, not_52_out, S0, R_Type, not_53_out, not_54_out, not_55_out, not_56_out, not_57_out, not_58_out, not_59_out);
  and and_10 (and_10_out, not_60_out, not_61_out, not_62_out, S0, not_63_out, not_64_out, not_65_out, SW, not_66_out, not_67_out, not_68_out, not_69_out);
  and and_11 (and_11_out, not_70_out, not_71_out, not_72_out, S0, not_73_out, not_74_out, not_75_out, not_76_out, not_77_out, not_78_out, SYSCALL, not_79_out);
  and and_12 (and_12_out, not_80_out, not_81_out, S1, S0);
  and and_13 (and_13_out, not_82_out, S2, not_83_out, S0);
  and and_14 (and_14_out, S3, not_84_out, S1, S0);
  and and_15 (and_15_out, S3, S2, not_85_out, S0);
  and and_16 (and_16_out, not_86_out, not_87_out, not_88_out, S0, not_89_out, not_90_out, not_91_out, J);
  and and_17 (and_17_out, not_92_out, not_93_out, not_94_out, S0, R_Type, not_95_out, not_96_out, not_97_out, not_98_out, not_99_out, not_100_out, not_101_out);
  and and_18 (and_18_out, not_102_out, not_103_out, not_104_out, S0, not_105_out, I_Type, not_106_out, not_107_out, not_108_out, not_109_out, not_110_out, not_111_out);
  and and_19 (and_19_out, not_112_out, not_113_out, not_114_out, S0, not_115_out, not_116_out, LW, not_117_out, not_118_out, not_119_out, not_120_out, not_121_out);
  and and_20 (and_20_out, not_122_out, not_123_out, not_124_out, S0, not_125_out, not_126_out, not_127_out, not_128_out, not_129_out, BNE, not_130_out, not_131_out);
  and and_21 (and_21_out, not_132_out, not_133_out, S1, not_134_out);
  and and_22 (and_22_out, not_135_out, S2, not_136_out, S0);
  and and_23 (and_23_out, not_137_out, not_138_out, not_139_out, S0, not_140_out, not_141_out, not_142_out, J);
  and and_24 (and_24_out, not_143_out, not_144_out, not_145_out, not_146_out);
  and and_25 (and_25_out, not_147_out, not_148_out, not_149_out, S0, R_Type, not_150_out, not_151_out, not_152_out, not_153_out, not_154_out, not_155_out, not_156_out);
  and and_26 (and_26_out, not_157_out, not_158_out, not_159_out, S0, not_160_out, I_Type, not_161_out, not_162_out, not_163_out, not_164_out, not_165_out, not_166_out);
  and and_27 (and_27_out, not_167_out, not_168_out, not_169_out, S0, not_170_out, not_171_out, not_172_out, SW, not_173_out, not_174_out, not_175_out, not_176_out);
  and and_28 (and_28_out, not_177_out, not_178_out, not_179_out, S0, not_180_out, not_181_out, not_182_out, not_183_out, BEQ, not_184_out, not_185_out, not_186_out);
  and and_29 (and_29_out, not_187_out, not_188_out, not_189_out, S0, not_190_out, not_191_out, not_192_out, not_193_out, not_194_out, not_195_out, SYSCALL, not_196_out);
  and and_30 (and_30_out, not_197_out, not_198_out, S1, not_199_out);
  and and_31 (and_31_out, S3, S2, not_200_out, S0);
  and and_32 (and_32_out, not_201_out, not_202_out, not_203_out, S0, not_204_out, not_205_out, not_206_out, J);
  or or_1 (N3, and_1_out, and_2_out, and_3_out, and_4_out, and_5_out, and_6_out, and_7_out, and_8_out);
  or or_2 (N2, and_9_out, and_10_out, and_11_out, and_12_out, and_13_out, and_14_out, and_15_out, and_16_out);
  or or_3 (N1, and_17_out, and_18_out, and_19_out, and_20_out, and_21_out, and_22_out, and_23_out);
  or or_4 (N0, and_24_out, and_25_out, and_26_out, and_27_out, and_28_out, and_29_out, and_30_out, and_31_out, and_32_out);
endmodule

module _4in16outCtrl (
  input  [5:0] OP,
  input  [5:0] Func,
  input  CLK,
  input  RST,
  output [3:0] ALU_OP,
  output Bne,
  output Beq,
  output MemRead,
  output MemWrite,
  output RegWrite,
  output PcWrite,
  output IrWrite,
  output RegDst,
  output MemToReg,
  output [3:0] \当前状态 ,
  output [1:0] AluSrcB,
  output AluSrcA,
  output PCsrc,
  output IorD
);

  wire ADD, ADDI, AND, ANDI, BEQ_t, BNE_t, comparator_6_eq, comparator_9_eq, comparator_10_eq,
       comparator_11_eq, comparator_12_eq, I_TYPE, J, LW, or_3_out, or_4_out, R_TYPE, SLT, SW, SysCall;
  wire [1:0] ALU_Control;
  wire [3:0] controlled_buffer_1_out, fsm_1_n0;

  Comparator #(.width(6), .mode("twosComplement")) comparator_1 (.a(OP), .b(6'b100011), .eq(LW));  // open: gt, lt
  Comparator #(.width(6), .mode("twosComplement")) comparator_2 (.a(OP), .b(6'b101011), .eq(SW));  // open: gt, lt
  Comparator #(.width(6), .mode("twosComplement")) comparator_3 (.a(OP), .b(6'b000100), .eq(BEQ_t));  // open: gt, lt
  Comparator #(.width(6), .mode("twosComplement")) comparator_4 (.a(OP), .b(6'b000101), .eq(BNE_t));  // open: gt, lt
  Comparator #(.width(6), .mode("twosComplement")) comparator_5 (.a(OP), .b(6'b001000), .eq(ADDI));  // open: gt, lt
  Comparator #(.width(6), .mode("twosComplement")) comparator_6 (
    .a(OP), .b({6{1'b0}}), .eq(comparator_6_eq));  // open: gt, lt
  Comparator #(.width(6), .mode("twosComplement")) comparator_7 (.a(OP), .b(6'b000010), .eq(J));  // open: gt, lt
  Comparator #(.width(6), .mode("twosComplement")) comparator_8 (.a(OP), .b(6'b001100), .eq(ANDI));  // open: gt, lt
  FSM fsm_1 (
    .S3(\当前状态 [3]), .S2(\当前状态 [2]), .S1(\当前状态 [1]), .S0(\当前状态 [0]), .R_Type(R_TYPE), .I_Type(I_TYPE),
    .LW(LW), .SW(SW), .BEQ(BEQ_t), .BNE(BNE_t), .SYSCALL(SysCall), .J(J), .N3(fsm_1_n0[3]), .N2(fsm_1_n0[2]),
    .N1(fsm_1_n0[1]), .N0(fsm_1_n0[0]));
  Comparator #(.width(6), .mode("twosComplement")) comparator_9 (
    .a(Func), .b(6'b100000), .eq(comparator_9_eq));  // open: gt, lt
  Comparator #(.width(6), .mode("twosComplement")) comparator_10 (
    .a(Func), .b(6'b101010), .eq(comparator_10_eq));  // open: gt, lt
  Comparator #(.width(6), .mode("twosComplement")) comparator_11 (
    .a(Func), .b(6'b001100), .eq(comparator_11_eq));  // open: gt, lt
  Comparator #(.width(6), .mode("twosComplement")) comparator_12 (
    .a(Func), .b(6'b100100), .eq(comparator_12_eq));  // open: gt, lt
  or or_1 (R_TYPE, ADD, SLT);
  and and_1 (ADD, comparator_9_eq, comparator_6_eq);
  and and_2 (SLT, comparator_10_eq, comparator_6_eq);
  and and_3 (SysCall, comparator_11_eq, comparator_6_eq);
  and and_4 (AND, comparator_12_eq, comparator_6_eq);
  or or_2 (I_TYPE, ANDI, ADDI);
  Register #(.width(4), .trigger("rising"), .Select("low")) register_1 (
    .D(fsm_1_n0), .Q(\当前状态 ), .clk(CLK), .clr(RST));  // open: en
  \封装4_16  \u_封装4_16_1  (
    .in_1(\当前状态 ),
    .out_2({IorD, PCsrc, AluSrcA, AluSrcB, MemToReg, RegDst, IrWrite, PcWrite, RegWrite, MemWrite, MemRead, Beq, Bne, ALU_Control}));
  assign controlled_buffer_1_out = or_3_out ? 4'b0101 : 4'bz;  // Controlled_Buffer controlled_buffer_1
  or or_3 (or_3_out, ADDI, ADD);
  assign controlled_buffer_1_out = or_4_out ? 4'b0111 : 4'bz;  // Controlled_Buffer controlled_buffer_2
  or or_4 (or_4_out, AND, ANDI);
  assign controlled_buffer_1_out = SLT ? 4'b1011 : 4'bz;  // Controlled_Buffer controlled_buffer_3
  Multiplexer #(.select(2), .width(4), .disabled("Z"), .enable("false")) multiplexer_1 (
    .in0(4'b0101), .in1(4'b0110), .in2(controlled_buffer_1_out), .out(ALU_OP), .sel(ALU_Control));  // open: in3

  // Notes on the sheet:
  //   指令译码信号
  //   现态
  //   组合逻辑
  //   指令译码逻辑
  //   次态
  //   状态寄存器
  //   ALU控制器逻辑
  //   根据ALU_Control的值决定运算器运算选择控制信号ALU_OP的值
  //   ALU_Control= 00 运算器做加法
  //   ALU_Control= 01 运算器做减法
  //   ALU_Control= 10 运算方式由Func决定 
endmodule

module \封装4_16  (
  input  [3:0] in_1,
  output [15:0] out_2
);

  _4in16out u_4in16out_1 (
    .S3(in_1[3]), .S2(in_1[2]), .S1(in_1[1]), .S0(in_1[0]), .IorD(out_2[15]), .PcSrc(out_2[14]),
    .AluSrcA(out_2[13]), .AluSrcB1(out_2[12]), .AluSrcB2(out_2[11]), .MemToReg(out_2[10]), .RegDst(out_2[9]),
    .IrWrite(out_2[8]), .PcWrite(out_2[7]), .RegWrite(out_2[6]), .MemWrite(out_2[5]), .MemRead(out_2[4]),
    .BEQ(out_2[3]), .BNE(out_2[2]), .AluControl1(out_2[1]), .AluControl2(out_2[0]));
endmodule

module _4in16out (
  input  S3,
  input  S2,
  input  S1,
  input  S0,
  output IorD,
  output PcSrc,
  output AluSrcA,
  output AluSrcB1,
  output AluSrcB2,
  output MemToReg,
  output RegDst,
  output IrWrite,
  output PcWrite,
  output RegWrite,
  output MemWrite,
  output MemRead,
  output BEQ,
  output BNE,
  output AluControl1,
  output AluControl2
);

  wire and_1_out, and_2_out, and_3_out, and_4_out, and_5_out, and_6_out, and_7_out, and_8_out, and_9_out,
       and_10_out, and_11_out, and_12_out, and_13_out, and_14_out, and_15_out, and_16_out, and_17_out,
       and_18_out, and_19_out, and_23_out, and_24_out, and_25_out, and_26_out, and_27_out, and_29_out,
       and_30_out, and_33_out, and_34_out, and_35_out, and_36_out, and_37_out, not_1_out, not_2_out,
       not_3_out, not_4_out, not_5_out, not_6_out, not_7_out, not_8_out, not_9_out, not_10_out, not_11_out,
       not_12_out, not_13_out, not_14_out, not_15_out, not_16_out, not_17_out, not_18_out, not_19_out,
       not_20_out, not_21_out, not_22_out, not_23_out, not_24_out, not_25_out, not_26_out, not_27_out,
       not_28_out, not_29_out, not_30_out, not_31_out, not_32_out, not_33_out, not_34_out, not_35_out,
       not_36_out, not_37_out, not_38_out, not_39_out, not_40_out, not_41_out, not_42_out, not_43_out,
       not_44_out, not_45_out, not_46_out, not_47_out, not_48_out, not_49_out, not_50_out, not_51_out,
       not_52_out, not_53_out, not_54_out, not_55_out, not_56_out, not_57_out, not_58_out, not_59_out,
       not_60_out, not_61_out, not_62_out, not_63_out, not_64_out, not_65_out, not_66_out, not_67_out,
       not_68_out, not_69_out, not_70_out, not_71_out, not_72_out, not_73_out, not_74_out, not_75_out;

  not not_1 (not_1_out, S3);
  not not_2 (not_2_out, S2);
  not not_3 (not_3_out, S3);
  not not_4 (not_4_out, S0);
  not not_5 (not_5_out, S2);
  not not_6 (not_6_out, S1);
  not not_7 (not_7_out, S2);
  not not_8 (not_8_out, S0);
  not not_9 (not_9_out, S3);
  not not_10 (not_10_out, S2);
  not not_11 (not_11_out, S0);
  not not_12 (not_12_out, S3);
  not not_13 (not_13_out, S1);
  not not_14 (not_14_out, S3);
  not not_15 (not_15_out, S2);
  not not_16 (not_16_out, S1);
  not not_17 (not_17_out, S2);
  not not_18 (not_18_out, S0);
  not not_19 (not_19_out, S2);
  not not_20 (not_20_out, S3);
  not not_21 (not_21_out, S2);
  not not_22 (not_22_out, S1);
  not not_23 (not_23_out, S3);
  not not_24 (not_24_out, S2);
  not not_25 (not_25_out, S0);
  not not_26 (not_26_out, S3);
  not not_27 (not_27_out, S1);
  not not_28 (not_28_out, S2);
  not not_29 (not_29_out, S3);
  not not_30 (not_30_out, S2);
  not not_31 (not_31_out, S1);
  not not_32 (not_32_out, S0);
  not not_33 (not_33_out, S3);
  not not_34 (not_34_out, S2);
  not not_35 (not_35_out, S1);
  not not_36 (not_36_out, S3);
  not not_37 (not_37_out, S1);
  not not_38 (not_38_out, S0);
  not not_39 (not_39_out, S2);
  not not_40 (not_40_out, S1);
  not not_41 (not_41_out, S0);
  not not_42 (not_42_out, S3);
  not not_43 (not_43_out, S2);
  not not_44 (not_44_out, S1);
  not not_45 (not_45_out, S0);
  not not_46 (not_46_out, S3);
  not not_47 (not_47_out, S2);
  not not_48 (not_48_out, S1);
  not not_49 (not_49_out, S0);
  not not_50 (not_50_out, S3);
  not not_51 (not_51_out, S1);
  not not_52 (not_52_out, S0);
  not not_53 (not_53_out, S2);
  not not_54 (not_54_out, S1);
  not not_55 (not_55_out, S0);
  not not_56 (not_56_out, S1);
  not not_57 (not_57_out, S0);
  not not_58 (not_58_out, S3);
  not not_59 (not_59_out, S0);
  not not_60 (not_60_out, S3);
  not not_61 (not_61_out, S2);
  not not_62 (not_62_out, S1);
  not not_63 (not_63_out, S0);
  not not_64 (not_64_out, S3);
  not not_65 (not_65_out, S2);
  not not_66 (not_66_out, S2);
  not not_67 (not_67_out, S1);
  not not_68 (not_68_out, S2);
  not not_69 (not_69_out, S0);
  not not_70 (not_70_out, S3);
  not not_71 (not_71_out, S2);
  not not_72 (not_72_out, S1);
  not not_73 (not_73_out, S2);
  not not_74 (not_74_out, S0);
  not not_75 (not_75_out, S2);
  and and_1 (and_1_out, not_1_out, not_2_out, S1, S0);
  and and_2 (and_2_out, not_3_out, S2, S1, not_4_out);
  and and_3 (and_3_out, S3, not_5_out, not_6_out, S0);
  and and_4 (and_4_out, S3, not_7_out, S1, not_8_out);
  and and_5 (and_5_out, S3, S2, S1, S0);
  and and_6 (and_6_out, not_9_out, not_10_out, S1, not_11_out);
  and and_7 (and_7_out, not_12_out, S2, not_13_out, S0);
  and and_8 (and_8_out, not_14_out, S2, S1, S0);
  and and_9 (and_9_out, S3, not_15_out, not_16_out, S0);
  and and_10 (and_10_out, S3, not_17_out, S1, not_18_out);
  and and_11 (and_11_out, S3, not_19_out, S1, S0);
  and and_12 (and_12_out, S3, S2, S1, S0);
  and and_13 (and_13_out, not_20_out, not_21_out, not_22_out, S0);
  and and_14 (and_14_out, not_23_out, not_24_out, S1, not_25_out);
  and and_15 (and_15_out, not_26_out, S2, not_27_out, S0);
  and and_16 (and_16_out, S3, not_28_out, S1, S0);
  and and_17 (and_17_out, S3, S2, S1, S0);
  and and_18 (and_18_out, not_29_out, not_30_out, not_31_out, not_32_out);
  and and_19 (and_19_out, not_33_out, not_34_out, not_35_out, S0);
  and and_20 (MemToReg, not_36_out, S2, not_37_out, not_38_out);
  and and_21 (RegDst, S3, not_39_out, not_40_out, not_41_out);
  and and_22 (IrWrite, not_42_out, not_43_out, not_44_out, not_45_out);
  and and_23 (and_23_out, not_46_out, not_47_out, not_48_out, not_49_out);
  and and_24 (and_24_out, S3, S2, S1, S0);
  and and_25 (and_25_out, not_50_out, S2, not_51_out, not_52_out);
  and and_26 (and_26_out, S3, not_53_out, not_54_out, not_55_out);
  and and_27 (and_27_out, S3, S2, not_56_out, not_57_out);
  and and_28 (MemWrite, not_58_out, S2, S1, not_59_out);
  and and_29 (and_29_out, not_60_out, not_61_out, not_62_out, not_63_out);
  and and_30 (and_30_out, not_64_out, not_65_out, S1, S0);
  and and_31 (BEQ, S3, not_66_out, not_67_out, S0);
  and and_32 (BNE, S3, not_68_out, S1, not_69_out);
  and and_33 (and_33_out, not_70_out, S2, S1, S0);
  and and_34 (and_34_out, S3, not_71_out, not_72_out, S0);
  and and_35 (and_35_out, S3, not_73_out, S1, not_74_out);
  and and_36 (and_36_out, S3, not_75_out, S1, S0);
  and and_37 (and_37_out, S3, S2, S1, S0);
  or or_1 (IorD, and_1_out, and_2_out);
  or or_2 (PcSrc, and_3_out, and_4_out, and_5_out);
  or or_3 (AluSrcA, and_6_out, and_7_out, and_8_out, and_9_out, and_10_out, and_11_out, and_12_out);
  or or_4 (AluSrcB1, and_13_out, and_14_out, and_15_out, and_16_out, and_17_out);
  or or_5 (AluSrcB2, and_18_out, and_19_out);
  or or_6 (PcWrite, and_23_out, and_24_out);
  or or_7 (RegWrite, and_25_out, and_26_out, and_27_out);
  or or_8 (MemRead, and_29_out, and_30_out);
  or or_9 (AluControl1, and_33_out, and_34_out, and_35_out, and_36_out, and_37_out);

  assign AluControl2 = 1'b0;
endmodule

module MIPS_Regifile (
  input  [31:0] Din,
  input  Clk,
  input  WE,
  input  [4:0] R1_num,
  input  [4:0] W_num,
  input  [4:0] R2_num,
  output [31:0] R1,
  output [31:0] R2
);

  // RegisterFile registerfile_1: pin names not known; wires that end beside it: Din, Clk, WE, W_num, R1_num, R2_num, R1, R2
endmodule

// ALU
module MIPS_ALU (
  input  [31:0] X,
  input  [31:0] Y,
  input  [3:0] AluOP,
  output Equal,
  output [31:0] Result,
  output [31:0] Result_2
);

  wire [0:0] comparator_1_lt, comparator_2_lt;
  wire [31:0] adder_1_out, AND_out, divider_1_out, divider_1_rem, multiplier_1_cout, multiplier_1_out,
       NOR_out, OR_out, shifter_1_out, shifter_2_out, shifter_3_out, subtractor_1_out, XOR_out;

  assign AND_out = X & Y;  // AND_Gate AND, 32 bits wide
  assign OR_out = X | Y;  // OR_Gate OR, 32 bits wide
  Shifter #(.width(32), .shift("ll")) shifter_1 (.in(X), .\dist (Y[4:0]), .out(shifter_1_out));
  Shifter #(.width(32), .shift("ar")) shifter_2 (.in(X), .\dist (Y[4:0]), .out(shifter_2_out));
  Shifter #(.width(32), .shift("lr")) shifter_3 (.in(X), .\dist (Y[4:0]), .out(shifter_3_out));
  Multiplier #(.width(32)) multiplier_1 (.a(X), .b(Y), .out(multiplier_1_out), .cout(multiplier_1_cout));  // open: cin
  Divider #(.width(32)) divider_1 (.a(X), .b(Y), .out(divider_1_out), .rem(divider_1_rem));  // open: upper
  Adder #(.width(32)) adder_1 (.a(X), .b(Y), .out(adder_1_out));  // open: cin, cout
  Subtractor #(.width(32)) subtractor_1 (.a(X), .b(Y), .out(subtractor_1_out));  // open: bin, bout
  assign XOR_out = X ^ Y;  // XOR_Gate XOR, 32 bits wide
  assign NOR_out = ~(X | Y);  // NOR_Gate NOR, 32 bits wide
  Comparator #(.width(32), .mode("twosComplement")) comparator_1 (
    .a(X), .b(Y), .eq(Equal), .lt(comparator_1_lt[0]));  // open: gt
  Comparator #(.width(32), .mode("unsigned")) comparator_2 (.a(X), .b(Y), .lt(comparator_2_lt[0]));  // open: gt, eq
  Multiplexer #(.select(4), .width(32), .disabled("Z"), .enable("false")) multiplexer_1 (
    .in0(shifter_1_out), .in1(shifter_2_out), .in2(shifter_3_out), .in3(multiplier_1_out),
    .in4(divider_1_out), .in5(adder_1_out), .in6(subtractor_1_out), .in7(AND_out), .in8(OR_out),
    .in9(XOR_out), .in10(NOR_out), .in11({{31{1'b0}}, comparator_1_lt[0]}),
    .in12({{31{1'b0}}, comparator_2_lt[0]}), .in13({32{1'b0}}), .in14({32{1'b0}}), .in15({32{1'b0}}),
    .out(Result), .sel(AluOP));
  Multiplexer #(.select(4), .width(32), .disabled("Z"), .enable("false")) multiplexer_2 (
    .in0({32{1'b0}}), .in1({32{1'b0}}), .in2({32{1'b0}}), .in3(multiplier_1_cout), .in4(divider_1_rem),
    .in5({32{1'b0}}), .in6({32{1'b0}}), .in7({32{1'b0}}), .in8({32{1'b0}}), .in9({32{1'b0}}),
    .in10({32{1'b0}}), .in11({32{1'b0}}), .in12({32{1'b0}}), .in13({32{1'b0}}), .in14({32{1'b0}}),
    .in15({32{1'b0}}), .out(Result_2), .sel(AluOP));

  // Other names for the same wires on the sheet: Result2[31:0] = Result_2; S[3:0] = AluOP

  // Notes on the sheet:
  //   不要改变此引脚区域内容，也不要改变ALU封装形式
  //   输入引脚
  //   X<Y为1
  //   输出引脚
  //   5为+
  //   6为-
  //   b为11比大小
endmodule
