// Logisim project 251124.circ as structural Verilog: 6 circuits, main circuit ◇单周期MIPS
module \单周期MIPS  (
  input  IR1,
  input  IR2,
  input  IR3,
  output RegWrite,
  output MemWrite,
  output [31:0] PC,
  output [31:0] IR,
  output [31:0] RDin,
  output [31:0] MDin,
  output [31:0] LedData
);

  wire and_1_out, and_2_out, and_3_out, BGTZ, CLK, comparator_1_gt, comparator_2_eq, Go, halt, IR1_t, IR2_t,
       IR3_t, IRA, IRB, IRC, LB, Ledout, mips_alu_1_equal, not_1_out, not_2_out, or_4_out, RST, SignedExt,
       SRLV, Syscall, W1, W2, W3, \单周期硬布线控制器_1_alu_src , \单周期硬布线控制器_1_beq , \单周期硬布线控制器_1_bne ,
       \单周期硬布线控制器_1_jal , \单周期硬布线控制器_1_jmp , \单周期硬布线控制器_1_jr , \单周期硬布线控制器_1_memtoreg , \单周期硬布线控制器_1_regdst ;
  wire [1:0] mode;
  wire [3:0] \单周期硬布线控制器_1_alu_op ;
  wire [4:0] multiplexer_4_out, multiplexer_5_out, multiplexer_6_out, multiplexer_7_out, multiplexer_10_out;
  wire [15:0] \总周期数 ;
  wire [31:0] adder_2_out, bit_extender_1_out, bit_extender_2_out, bit_extender_3_out, mips_alu_1_result,
       mips_ram_1_dataout, multiplexer_1_out, multiplexer_2_out, multiplexer_3_out, multiplexer_8_out,
       multiplexer_9_out, multiplexer_11_out, multiplexer_12_out, multiplexer_13_out, PC_4, R1Data,
       shifter_1_out;

  Clock #(.highDuration(1), .lowDuration(1)) clock_1 (.out(CLK));
  Button _1 (.out(IRA));
  Button _2 (.out(IRB));
  Button _3 (.out(IRC));
  Button \u_继续运行  (.out(Go));
  LED #(.active("true")) led_1 (.in(W1));
  LED #(.active("true")) led_2 (.in(W2));
  LED #(.active("true")) led_3 (.in(W3));
  Multiplexer #(.select(1), .width(32), .disabled("Z"), .enable("false")) multiplexer_1 (
    .in0(PC_4), .in1(adder_2_out), .out(multiplexer_1_out), .sel(or_4_out));
  Multiplexer #(.select(1), .width(32), .disabled("Z"), .enable("false")) multiplexer_2 (
    .in0(multiplexer_1_out), .in1({PC_4[31:28], IR[25:0], 2'b00}), .out(multiplexer_2_out),
    .sel(\单周期硬布线控制器_1_jmp ));
  Hex_Digit_Display hex_digit_display_1 (.value(LedData[31:28]));  // open: dp
  Multiplexer #(.select(1), .width(32), .disabled("Z"), .enable("false")) multiplexer_3 (
    .in0(multiplexer_2_out), .in1(R1Data), .out(multiplexer_3_out), .sel(\单周期硬布线控制器_1_jr ));
  Hex_Digit_Display hex_digit_display_2 (.value(LedData[23:20]));  // open: dp
  Hex_Digit_Display hex_digit_display_3 (.value(LedData[27:24]));  // open: dp
  not not_1 (not_1_out, halt);
  Hex_Digit_Display hex_digit_display_4 (.value(LedData[15:12]));  // open: dp
  Hex_Digit_Display hex_digit_display_5 (.value(LedData[19:16]));  // open: dp
  Register #(.width(32), .trigger("rising"), .Select("low")) u_PC (
    .D(multiplexer_3_out), .en(not_1_out), .Q(PC), .clk(CLK), .clr(RST));
  Adder #(.width(32)) adder_1 (.a(PC), .b(32'h4), .out(PC_4));  // open: cin, cout
  Hex_Digit_Display hex_digit_display_6 (.value(LedData[11:8]));  // open: dp
  Hex_Digit_Display hex_digit_display_7 (.value(LedData[7:4]));  // open: dp
  // Probe on \总周期数 
  Counter #(.width(16), .max('hffff), .ongoal("stay"), .trigger("rising"), .behavior("old")) counter_1 (
    .count(not_2_out), .Q(\总周期数 ), .clk(CLK));  // open: load, D, carry, clr, preset
  not not_2 (not_2_out, halt);
  // Mips_Probe mips_probe_1: pin names not known; wires that end beside it: IR
  Hex_Digit_Display hex_digit_display_8 (.value(LedData[3:0]));  // open: dp
  ROM #(.addrWidth(10), .dataWidth(32), .Select("high")) rom_1 (.addr(PC[11:2]), .data(IR));
  or or_1 (IR1_t, IR1, IRA);
  or or_2 (IR2_t, IR2, IRB);
  \单周期硬布线控制器  \u_单周期硬布线控制器_1  (
    .Func(IR[5:0]), .OP(IR[31:26]), .ALU_OP(\单周期硬布线控制器_1_alu_op ), .MemToReg(\单周期硬布线控制器_1_memtoreg ),
    .MemWrite(MemWrite), .ALU_SRC(\单周期硬布线控制器_1_alu_src ), .RegWrite(RegWrite), .SysCALL(Syscall),
    .SignedExt(SignedExt), .RegDst(\单周期硬布线控制器_1_regdst ), .JR(\单周期硬布线控制器_1_jr ), .JMP(\单周期硬布线控制器_1_jmp ),
    .Beq(\单周期硬布线控制器_1_beq ), .JAL(\单周期硬布线控制器_1_jal ), .Bne(\单周期硬布线控制器_1_bne ), .SRLV(SRLV), .LB(LB),
    .BGTZ(BGTZ), .Mode(mode));
  Multiplexer #(.select(1), .width(5), .disabled("Z"), .enable("false")) multiplexer_4 (
    .in0(IR[25:21]), .in1(5'b00010), .out(multiplexer_4_out), .sel(Syscall));
  Multiplexer #(.select(1), .width(5), .disabled("Z"), .enable("false")) multiplexer_5 (
    .in0(IR[20:16]), .in1(5'b00100), .out(multiplexer_5_out), .sel(Syscall));
  Multiplexer #(.select(1), .width(5), .disabled("Z"), .enable("false")) multiplexer_6 (
    .in0(IR[20:16]), .in1(IR[15:11]), .out(multiplexer_6_out), .sel(\单周期硬布线控制器_1_regdst ));
  Multiplexer #(.select(1), .width(5), .disabled("Z"), .enable("false")) multiplexer_7 (
    .in0(multiplexer_6_out), .in1({5{1'b1}}), .out(multiplexer_7_out), .sel(\单周期硬布线控制器_1_jal ));
  assign bit_extender_1_out = {{16{1'b0}}, IR[15:0]};  // Bit_Extender bit_extender_1
  assign bit_extender_2_out = {{16{IR[15]}}, IR[15:0]};  // Bit_Extender bit_extender_2
  or or_3 (IR3_t, IR3, IRC);
  Multiplexer #(.select(1), .width(32), .disabled("Z"), .enable("false")) multiplexer_8 (
    .in0(bit_extender_1_out), .in1(bit_extender_2_out), .out(multiplexer_8_out), .sel(SignedExt));
  Shifter #(.width(32), .shift("ll")) shifter_1 (.in(bit_extender_2_out), .\dist (5'b00010), .out(shifter_1_out));
  MIPS_Regifile mips_regifile_1 (
    .Din(multiplexer_13_out), .Clk(CLK), .R1(R1Data), .R2(MDin), .WE(RegWrite), .W_num(multiplexer_7_out),
    .R1_num(multiplexer_4_out), .R2_num(multiplexer_5_out));
  Adder #(.width(32)) adder_2 (.a(shifter_1_out), .b(PC_4), .out(adder_2_out));  // open: cin, cout
  Multiplexer #(.select(1), .width(32), .disabled("Z"), .enable("false")) multiplexer_9 (
    .in0(MDin), .in1(multiplexer_8_out), .out(multiplexer_9_out), .sel(\单周期硬布线控制器_1_alu_src ));
  Multiplexer #(.select(1), .width(5), .disabled("Z"), .enable("false")) multiplexer_10 (
    .in0(IR[10:6]), .in1(R1Data[4:0]), .out(multiplexer_10_out), .sel(SRLV));
  Comparator #(.width(32), .mode("twosComplement")) comparator_1 (
    .a(R1Data), .b({32{1'b0}}), .gt(comparator_1_gt));  // open: eq, lt
  and and_1 (and_1_out, comparator_1_gt, BGTZ);
  and and_2 (and_2_out, mips_alu_1_equal, \单周期硬布线控制器_1_beq );
  and and_3 (and_3_out, ~mips_alu_1_equal, \单周期硬布线控制器_1_bne );  // AND_Gate
  MIPS_ALU mips_alu_1 (
    .X(R1Data), .Y(multiplexer_9_out), .AluOP(\单周期硬布线控制器_1_alu_op ), .Equal(mips_alu_1_equal),
    .Result(mips_alu_1_result), .shamt(multiplexer_10_out));  // open: Result_2
  or or_4 (or_4_out, and_2_out, and_1_out, and_3_out);
  MIPS_RAM mips_ram_1 (
    .\字节地址 (mips_alu_1_result[11:0]), .Din(MDin), .DataOut(mips_ram_1_dataout), .CLK(CLK), .WE(MemWrite),
    .Mode(mode));
  Register #(.width(32), .trigger("rising"), .Select("low")) register_1 (
    .D(MDin), .en(Ledout), .Q(LedData), .clk(CLK));  // open: clr
  Multiplexer #(.select(1), .width(32), .disabled("Z"), .enable("false")) multiplexer_11 (
    .in0(mips_alu_1_result), .in1(mips_ram_1_dataout), .out(multiplexer_11_out), .sel(\单周期硬布线控制器_1_memtoreg ));
  Multiplexer #(.select(1), .width(32), .disabled("Z"), .enable("false")) multiplexer_12 (
    .in0(multiplexer_11_out), .in1(PC_4), .out(multiplexer_12_out), .sel(\单周期硬布线控制器_1_jal ));
  Comparator #(.width(32), .mode("twosComplement")) comparator_2 (
    .a(R1Data), .b(32'h22), .eq(comparator_2_eq));  // open: gt, lt
  assign bit_extender_3_out = {{24{multiplexer_12_out[7]}}, multiplexer_12_out[7:0]};  // Bit_Extender bit_extender_3
  Multiplexer #(.select(1), .width(32), .disabled("Z"), .enable("false")) multiplexer_13 (
    .in0(multiplexer_12_out), .in1(bit_extender_3_out), .out(multiplexer_13_out), .sel(LB));
  and and_4 (Ledout, Syscall, comparator_2_eq);
  and and_5 (halt, Syscall, ~Ledout);  // AND_Gate

  // Other names for the same wires on the sheet: OP[5:0] = IR[31:26]

  // Notes on the sheet:
  //   中断源
  //   中断等待指示
  //   总复位信号应将除ROM以外所有存储组件全部清零
  //   数码管输出
  //   数码管输出应该用寄存器锁存，否则显示数据只能一闪而过
  //   指令存储器
  //   contents of rom_1 (hex, n*v repeats v):
  //   20090000 200b0010 34118483 20120404 118c00 129400 36318281 22520404 ad310000 2328820 21290004
  //   216bffff 1560fffb 200b0020 20090000 81310000 112020 20020022 c 21290001 216bffff 1560fff9 2002000a c
  //   OP
  //   Func
  //   rs
  //   指令字
  //   rt
  //   rd
  //   JMP
  //   JR
  //   OP
  //   Func
  //   Beq
  //   Bne
  //   MemToReg
  //   MemWrite
  //   AluOP
  //   AluSrcB
  //   RegWrite
  //   JAL
  //   RegDst
  //   Syscall
  //   为方便自动评测，需要输出PC，IR，寄存器堆写如数据RDin
  //   bgtz扩展
  //   SRLV扩展
  //   RAM写使能MemWrite、RAM写入数据MDin等信号
  //   LB扩展
endmodule

// 单周期硬布线控制器
module \单周期硬布线控制器  (
  input  [5:0] OP,
  input  [5:0] Func,
  output [3:0] ALU_OP,
  output MemToReg,
  output MemWrite,
  output ALU_SRC,
  output RegWrite,
  output SysCALL,
  output SignedExt,
  output RegDst,
  output Beq,
  output Bne,
  output JR,
  output JMP,
  output JAL,
  output SRLV,
  output LB,
  output BGTZ,
  output [1:0] Mode
);

  \运算控制器自动生成  \u_运算控制器自动生成_1  (
    .OP0(OP[0]), .OP1(OP[1]), .OP2(OP[2]), .OP3(OP[3]), .OP4(OP[4]), .OP5(OP[5]), .F0(Func[0]), .F1(Func[1]),
    .F2(Func[2]), .F3(Func[3]), .F4(Func[4]), .F5(Func[5]), .S0(ALU_OP[0]), .S1(ALU_OP[1]), .S2(ALU_OP[2]),
    .S3(ALU_OP[3]));
  \控制信号自动生成  \u_控制信号自动生成_1  (
    .OP0(OP[0]), .OP1(OP[1]), .OP2(OP[2]), .OP3(OP[3]), .OP4(OP[4]), .OP5(OP[5]), .F0(Func[0]), .F1(Func[1]),
    .F2(Func[2]), .F3(Func[3]), .F4(Func[4]), .F5(Func[5]), .MemToReg(MemToReg), .MemWrite(MemWrite),
    .ALU_SRC(ALU_SRC), .RegWrite(RegWrite), .SysCALL(SysCALL), .SignedExt(SignedExt), .RegDst(RegDst),
    .BEQ(Beq), .BNE(Bne), .JR(JR), .JUMP(JMP), .JAL(JAL), .SRLV(SRLV), .LB(LB), .BGTZ(BGTZ), .mode1(Mode[1]),
    .mode2(Mode[0]));

  // Other names for the same wires on the sheet: OP_CODE[5:0] = OP

  // Notes on the sheet:
  //   运算器控制器，根据指令生成运算器功能选择信号
  //   控制信号生成，产生数据通路需要的其他控制信号
endmodule

// 运算器控制器
module \运算控制器自动生成  (
  input  OP0,
  input  OP1,
  input  OP2,
  input  OP3,
  input  OP4,
  input  OP5,
  input  F0,
  input  F1,
  input  F2,
  input  F3,
  input  F4,
  input  F5,
  output S0,
  output S1,
  output S2,
  output S3
);

  wire and_1_out, and_2_out, and_3_out, and_4_out, and_5_out, and_6_out, and_7_out, and_8_out, and_9_out,
       and_10_out, and_11_out, and_12_out, and_13_out, and_14_out, and_15_out, and_16_out, and_17_out,
       and_18_out, and_19_out, and_20_out, and_21_out, and_22_out, and_23_out, and_24_out, and_25_out,
       and_26_out, and_27_out, and_28_out, and_29_out, and_30_out, and_31_out, and_32_out, and_33_out,
       and_34_out, and_35_out, and_36_out, and_37_out, and_38_out, and_39_out, not_1_out, not_2_out,
       not_3_out, not_4_out, not_5_out, not_6_out, not_7_out, not_8_out, not_9_out, not_10_out, not_11_out,
       not_12_out, not_13_out, not_14_out, not_15_out, not_16_out, not_17_out, not_18_out, not_19_out,
       not_20_out, not_21_out, not_22_out, not_23_out, not_24_out, not_25_out, not_26_out, not_27_out,
       not_28_out, not_29_out, not_30_out, not_31_out, not_32_out, not_33_out, not_34_out, not_35_out,
       not_36_out, not_37_out, not_38_out, not_39_out, not_40_out, not_41_out, not_42_out, not_43_out,
       not_44_out, not_45_out, not_46_out, not_47_out, not_48_out, not_49_out, not_50_out, not_51_out,
       not_52_out, not_53_out, not_54_out, not_55_out, not_56_out, not_57_out, not_58_out, not_59_out,
       not_60_out, not_61_out, not_62_out, not_63_out, not_64_out, not_65_out, not_66_out, not_67_out,
       not_68_out, not_69_out, not_70_out, not_71_out, not_72_out, not_73_out, not_74_out, not_75_out,
       not_76_out, not_77_out, not_78_out, not_79_out, not_80_out, not_81_out, not_82_out, not_83_out,
       not_84_out, not_85_out, not_86_out, not_87_out, not_88_out, not_89_out, not_90_out, not_91_out,
       not_92_out, not_93_out, not_94_out, not_95_out, not_96_out, not_97_out, not_98_out, not_99_out,
       not_100_out, not_101_out, not_102_out, not_103_out, not_104_out, not_105_out, not_106_out,
       not_107_out, not_108_out, not_109_out, not_110_out, not_111_out, not_112_out, not_113_out,
       not_114_out, not_115_out, not_116_out, not_117_out, not_118_out, not_119_out, not_120_out,
       not_121_out, not_122_out, not_123_out, not_124_out, not_125_out, not_126_out, not_127_out,
       not_128_out, not_129_out, not_130_out, not_131_out, not_132_out, not_133_out, not_134_out,
       not_135_out, not_136_out, not_137_out, not_138_out, not_139_out, not_140_out, not_141_out,
       not_142_out, not_143_out, not_144_out, not_145_out, not_146_out, not_147_out, not_148_out,
       not_149_out, not_150_out, not_151_out, not_152_out, not_153_out, not_154_out, not_155_out,
       not_156_out, not_157_out, not_158_out, not_159_out, not_160_out, not_161_out, not_162_out,
       not_163_out, not_164_out, not_165_out, not_166_out, not_167_out, not_168_out, not_169_out,
       not_170_out, not_171_out, not_172_out, not_173_out, not_174_out, not_175_out, not_176_out,
       not_177_out, not_178_out, not_179_out, not_180_out, not_181_out, not_182_out, not_183_out,
       not_184_out, not_185_out, not_186_out, not_187_out, not_188_out, not_189_out, not_190_out,
       not_191_out, not_192_out, not_193_out, not_194_out, not_195_out, not_196_out, not_197_out,
       not_198_out, not_199_out, not_200_out, not_201_out, not_202_out, not_203_out, not_204_out,
       not_205_out, not_206_out, not_207_out, not_208_out, not_209_out, not_210_out, not_211_out,
       not_212_out, not_213_out, not_214_out, not_215_out, not_216_out, not_217_out, not_218_out,
       not_219_out, not_220_out, not_221_out, not_222_out, not_223_out, not_224_out, not_225_out,
       not_226_out, not_227_out, not_228_out, not_229_out, not_230_out, not_231_out, not_232_out,
       not_233_out, not_234_out, not_235_out, not_236_out, not_237_out, not_238_out, not_239_out,
       not_240_out, not_241_out, not_242_out, not_243_out, not_244_out, not_245_out, not_246_out,
       not_247_out, not_248_out, not_249_out, not_250_out, not_251_out, not_252_out, not_253_out,
       not_254_out, not_255_out, not_256_out, not_257_out, not_258_out, not_259_out, not_260_out,
       not_261_out, not_262_out, not_263_out, not_264_out, not_265_out, not_266_out, not_267_out,
       not_268_out, not_269_out, not_270_out, not_271_out, not_272_out, not_273_out, not_274_out;

  not not_1 (not_1_out, OP5);
  not not_2 (not_2_out, OP4);
  not not_3 (not_3_out, OP3);
  not not_4 (not_4_out, OP2);
  not not_5 (not_5_out, OP1);
  not not_6 (not_6_out, OP0);
  not not_7 (not_7_out, F5);
  not not_8 (not_8_out, F4);
  not not_9 (not_9_out, F3);
  not not_10 (not_10_out, F2);
  not not_11 (not_11_out, OP5);
  not not_12 (not_12_out, OP4);
  not not_13 (not_13_out, OP3);
  not not_14 (not_14_out, OP2);
  not not_15 (not_15_out, OP1);
  not not_16 (not_16_out, OP0);
  not not_17 (not_17_out, F4);
  not not_18 (not_18_out, F3);
  not not_19 (not_19_out, F2);
  not not_20 (not_20_out, F1);
  not not_21 (not_21_out, F0);
  not not_22 (not_22_out, OP5);
  not not_23 (not_23_out, OP4);
  not not_24 (not_24_out, OP3);
  not not_25 (not_25_out, OP2);
  not not_26 (not_26_out, OP1);
  not not_27 (not_27_out, OP0);
  not not_28 (not_28_out, F4);
  not not_29 (not_29_out, F3);
  not not_30 (not_30_out, F2);
  not not_31 (not_31_out, F1);
  not not_32 (not_32_out, OP5);
  not not_33 (not_33_out, OP4);
  not not_34 (not_34_out, OP3);
  not not_35 (not_35_out, OP2);
  not not_36 (not_36_out, OP1);
  not not_37 (not_37_out, OP0);
  not not_38 (not_38_out, F4);
  not not_39 (not_39_out, F3);
  not not_40 (not_40_out, F1);
  not not_41 (not_41_out, F0);
  not not_42 (not_42_out, OP5);
  not not_43 (not_43_out, OP4);
  not not_44 (not_44_out, OP3);
  not not_45 (not_45_out, OP2);
  not not_46 (not_46_out, OP1);
  not not_47 (not_47_out, OP0);
  not not_48 (not_48_out, F4);
  not not_49 (not_49_out, F2);
  not not_50 (not_50_out, F0);
  not not_51 (not_51_out, OP5);
  not not_52 (not_52_out, OP4);
  not not_53 (not_53_out, OP2);
  not not_54 (not_54_out, OP1);
  not not_55 (not_55_out, OP0);
  not not_56 (not_56_out, OP5);
  not not_57 (not_57_out, OP4);
  not not_58 (not_58_out, OP1);
  not not_59 (not_59_out, OP0);
  not not_60 (not_60_out, OP5);
  not not_61 (not_61_out, OP4);
  not not_62 (not_62_out, OP2);
  not not_63 (not_63_out, OP1);
  not not_64 (not_64_out, OP5);
  not not_65 (not_65_out, OP4);
  not not_66 (not_66_out, OP2);
  not not_67 (not_67_out, OP0);
  not not_68 (not_68_out, OP4);
  not not_69 (not_69_out, OP3);
  not not_70 (not_70_out, OP2);
  not not_71 (not_71_out, OP4);
  not not_72 (not_72_out, OP2);
  not not_73 (not_73_out, OP5);
  not not_74 (not_74_out, OP4);
  not not_75 (not_75_out, OP3);
  not not_76 (not_76_out, OP2);
  not not_77 (not_77_out, OP1);
  not not_78 (not_78_out, OP0);
  not not_79 (not_79_out, F4);
  not not_80 (not_80_out, F3);
  not not_81 (not_81_out, F0);
  not not_82 (not_82_out, OP4);
  not not_83 (not_83_out, OP3);
  not not_84 (not_84_out, OP2);
  not not_85 (not_85_out, OP1);
  not not_86 (not_86_out, OP0);
  not not_87 (not_87_out, OP5);
  not not_88 (not_88_out, OP4);
  not not_89 (not_89_out, OP3);
  not not_90 (not_90_out, OP2);
  not not_91 (not_91_out, OP1);
  not not_92 (not_92_out, OP0);
  not not_93 (not_93_out, F5);
  not not_94 (not_94_out, F4);
  not not_95 (not_95_out, F3);
  not not_96 (not_96_out, F2);
  not not_97 (not_97_out, F0);
  not not_98 (not_98_out, OP5);
  not not_99 (not_99_out, OP4);
  not not_100 (not_100_out, OP3);
  not not_101 (not_101_out, OP2);
  not not_102 (not_102_out, OP1);
  not not_103 (not_103_out, OP0);
  not not_104 (not_104_out, F4);
  not not_105 (not_105_out, F3);
  not not_106 (not_106_out, F2);
  not not_107 (not_107_out, F0);
  not not_108 (not_108_out, OP5);
  not not_109 (not_109_out, OP4);
  not not_110 (not_110_out, OP3);
  not not_111 (not_111_out, OP2);
  not not_112 (not_112_out, OP1);
  not not_113 (not_113_out, OP0);
  not not_114 (not_114_out, F4);
  not not_115 (not_115_out, F3);
  not not_116 (not_116_out, F1);
  not not_117 (not_117_out, F0);
  not not_118 (not_118_out, OP5);
  not not_119 (not_119_out, OP4);
  not not_120 (not_120_out, OP3);
  not not_121 (not_121_out, OP2);
  not not_122 (not_122_out, OP1);
  not not_123 (not_123_out, OP0);
  not not_124 (not_124_out, F4);
  not not_125 (not_125_out, F3);
  not not_126 (not_126_out, OP5);
  not not_127 (not_127_out, OP4);
  not not_128 (not_128_out, OP3);
  not not_129 (not_129_out, OP2);
  not not_130 (not_130_out, OP1);
  not not_131 (not_131_out, OP0);
  not not_132 (not_132_out, F4);
  not not_133 (not_133_out, F2);
  not not_134 (not_134_out, F0);
  not not_135 (not_135_out, OP5);
  not not_136 (not_136_out, OP4);
  not not_137 (not_137_out, OP1);
  not not_138 (not_138_out, OP0);
  not not_139 (not_139_out, OP5);
  not not_140 (not_140_out, OP4);
  not not_141 (not_141_out, OP2);
  not not_142 (not_142_out, OP0);
  not not_143 (not_143_out, OP5);
  not not_144 (not_144_out, OP4);
  not not_145 (not_145_out, OP3);
  not not_146 (not_146_out, OP2);
  not not_147 (not_147_out, OP1);
  not not_148 (not_148_out, OP0);
  not not_149 (not_149_out, F5);
  not not_150 (not_150_out, F4);
  not not_151 (not_151_out, F3);
  not not_152 (not_152_out, F0);
  not not_153 (not_153_out, OP5);
  not not_154 (not_154_out, OP4);
  not not_155 (not_155_out, OP3);
  not not_156 (not_156_out, OP2);
  not not_157 (not_157_out, OP1);
  not not_158 (not_158_out, OP0);
  not not_159 (not_159_out, F4);
  not not_160 (not_160_out, F3);
  not not_161 (not_161_out, F2);
  not not_162 (not_162_out, F1);
  not not_163 (not_163_out, F0);
  not not_164 (not_164_out, OP5);
  not not_165 (not_165_out, OP4);
  not not_166 (not_166_out, OP3);
  not not_167 (not_167_out, OP2);
  not not_168 (not_168_out, OP1);
  not not_169 (not_169_out, OP0);
  not not_170 (not_170_out, F4);
  not not_171 (not_171_out, F3);
  not not_172 (not_172_out, F2);
  not not_173 (not_173_out, F1);
  not not_174 (not_174_out, OP5);
  not not_175 (not_175_out, OP4);
  not not_176 (not_176_out, OP3);
  not not_177 (not_177_out, OP2);
  not not_178 (not_178_out, OP1);
  not not_179 (not_179_out, OP0);
  not not_180 (not_180_out, F4);
  not not_181 (not_181_out, F3);
  not not_182 (not_182_out, F2);
  not not_183 (not_183_out, F0);
  not not_184 (not_184_out, OP5);
  not not_185 (not_185_out, OP4);
  not not_186 (not_186_out, OP3);
  not not_187 (not_187_out, OP2);
  not not_188 (not_188_out, OP1);
  not not_189 (not_189_out, OP0);
  not not_190 (not_190_out, F4);
  not not_191 (not_191_out, F3);
  not not_192 (not_192_out, F1);
  not not_193 (not_193_out, F0);
  not not_194 (not_194_out, OP5);
  not not_195 (not_195_out, OP4);
  not not_196 (not_196_out, OP3);
  not not_197 (not_197_out, OP2);
  not not_198 (not_198_out, OP1);
  not not_199 (not_199_out, OP0);
  not not_200 (not_200_out, F4);
  not not_201 (not_201_out, F2);
  not not_202 (not_202_out, OP5);
  not not_203 (not_203_out, OP4);
  not not_204 (not_204_out, OP2);
  not not_205 (not_205_out, OP1);
  not not_206 (not_206_out, OP0);
  not not_207 (not_207_out, OP5);
  not not_208 (not_208_out, OP4);
  not not_209 (not_209_out, OP1);
  not not_210 (not_210_out, OP0);
  not not_211 (not_211_out, OP5);
  not not_212 (not_212_out, OP4);
  not not_213 (not_213_out, OP2);
  not not_214 (not_214_out, OP1);
  not not_215 (not_215_out, OP4);
  not not_216 (not_216_out, OP3);
  not not_217 (not_217_out, OP2);
  not not_218 (not_218_out, OP4);
  not not_219 (not_219_out, OP2);
  not not_220 (not_220_out, OP4);
  not not_221 (not_221_out, OP3);
  not not_222 (not_222_out, OP2);
  not not_223 (not_223_out, OP1);
  not not_224 (not_224_out, OP0);
  not not_225 (not_225_out, OP5);
  not not_226 (not_226_out, OP4);
  not not_227 (not_227_out, OP3);
  not not_228 (not_228_out, OP2);
  not not_229 (not_229_out, OP1);
  not not_230 (not_230_out, OP0);
  not not_231 (not_231_out, F4);
  not not_232 (not_232_out, F3);
  not not_233 (not_233_out, F1);
  not not_234 (not_234_out, OP5);
  not not_235 (not_235_out, OP4);
  not not_236 (not_236_out, OP3);
  not not_237 (not_237_out, OP2);
  not not_238 (not_238_out, OP1);
  not not_239 (not_239_out, OP0);
  not not_240 (not_240_out, F4);
  not not_241 (not_241_out, F3);
  not not_242 (not_242_out, OP5);
  not not_243 (not_243_out, OP4);
  not not_244 (not_244_out, OP3);
  not not_245 (not_245_out, OP2);
  not not_246 (not_246_out, OP1);
  not not_247 (not_247_out, OP0);
  not not_248 (not_248_out, F4);
  not not_249 (not_249_out, F2);
  not not_250 (not_250_out, F0);
  not not_251 (not_251_out, OP5);
  not not_252 (not_252_out, OP4);
  not not_253 (not_253_out, OP3);
  not not_254 (not_254_out, OP2);
  not not_255 (not_255_out, OP1);
  not not_256 (not_256_out, OP0);
  not not_257 (not_257_out, F4);
  not not_258 (not_258_out, F2);
  not not_259 (not_259_out, OP5);
  not not_260 (not_260_out, OP4);
  not not_261 (not_261_out, OP2);
  not not_262 (not_262_out, OP0);
  not not_263 (not_263_out, OP5);
  not not_264 (not_264_out, OP4);
  not not_265 (not_265_out, OP1);
  not not_266 (not_266_out, OP5);
  not not_267 (not_267_out, OP4);
  not not_268 (not_268_out, OP3);
  not not_269 (not_269_out, OP2);
  not not_270 (not_270_out, OP1);
  not not_271 (not_271_out, OP0);
  not not_272 (not_272_out, F4);
  not not_273 (not_273_out, F3);
  not not_274 (not_274_out, F0);
  and and_1 (and_1_out, not_1_out, not_2_out, not_3_out, not_4_out, not_5_out, not_6_out, not_7_out, not_8_out, not_9_out, not_10_out, F1, F0);
  and and_2 (and_2_out, not_11_out, not_12_out, not_13_out, not_14_out, not_15_out, not_16_out, F5, not_17_out, not_18_out, not_19_out, not_20_out, not_21_out);
  and and_3 (and_3_out, not_22_out, not_23_out, not_24_out, not_25_out, not_26_out, not_27_out, F5, not_28_out, not_29_out, not_30_out, not_31_out, F0);
  and and_4 (and_4_out, not_32_out, not_33_out, not_34_out, not_35_out, not_36_out, not_37_out, F5, not_38_out, not_39_out, F2, not_40_out, not_41_out);
  and and_5 (and_5_out, not_42_out, not_43_out, not_44_out, not_45_out, not_46_out, not_47_out, F5, not_48_out, F3, not_49_out, F1, not_50_out);
  and and_6 (and_6_out, not_51_out, not_52_out, OP3, not_53_out, not_54_out, not_55_out);
  and and_7 (and_7_out, not_56_out, not_57_out, OP3, OP2, not_58_out, not_59_out);
  and and_8 (and_8_out, not_60_out, not_61_out, OP3, not_62_out, not_63_out, OP0);
  and and_9 (and_9_out, not_64_out, not_65_out, OP3, not_66_out, OP1, not_67_out);
  and and_10 (and_10_out, OP5, not_68_out, not_69_out, not_70_out, OP1, OP0);
  and and_11 (and_11_out, OP5, not_71_out, OP3, not_72_out, OP1, OP0);
  and and_12 (and_12_out, not_73_out, not_74_out, not_75_out, not_76_out, not_77_out, not_78_out, F5, not_79_out, not_80_out, F2, F1, not_81_out);
  and and_13 (and_13_out, OP5, not_82_out, not_83_out, not_84_out, not_85_out, not_86_out);
  and and_14 (and_14_out, not_87_out, not_88_out, not_89_out, not_90_out, not_91_out, not_92_out, not_93_out, not_94_out, not_95_out, not_96_out, F1, not_97_out);
  and and_15 (and_15_out, not_98_out, not_99_out, not_100_out, not_101_out, not_102_out, not_103_out, F5, not_104_out, not_105_out, not_106_out, F1, not_107_out);
  and and_16 (and_16_out, not_108_out, not_109_out, not_110_out, not_111_out, not_112_out, not_113_out, F5, not_114_out, not_115_out, F2, not_116_out, not_117_out);
  and and_17 (and_17_out, not_118_out, not_119_out, not_120_out, not_121_out, not_122_out, not_123_out, F5, not_124_out, not_125_out, F2, F1, F0);
  and and_18 (and_18_out, not_126_out, not_127_out, not_128_out, not_129_out, not_130_out, not_131_out, F5, not_132_out, F3, not_133_out, F1, not_134_out);
  and and_19 (and_19_out, not_135_out, not_136_out, OP3, OP2, not_137_out, not_138_out);
  and and_20 (and_20_out, not_139_out, not_140_out, OP3, not_141_out, OP1, not_142_out);
  and and_21 (and_21_out, not_143_out, not_144_out, not_145_out, not_146_out, not_147_out, not_148_out, not_149_out, not_150_out, not_151_out, F2, F1, not_152_out);
  and and_22 (and_22_out, not_153_out, not_154_out, not_155_out, not_156_out, not_157_out, not_158_out, F5, not_159_out, not_160_out, not_161_out, not_162_out, not_163_out);
  and and_23 (and_23_out, not_164_out, not_165_out, not_166_out, not_167_out, not_168_out, not_169_out, F5, not_170_out, not_171_out, not_172_out, not_173_out, F0);
  and and_24 (and_24_out, not_174_out, not_175_out, not_176_out, not_177_out, not_178_out, not_179_out, F5, not_180_out, not_181_out, not_182_out, F1, not_183_out);
  and and_25 (and_25_out, not_184_out, not_185_out, not_186_out, not_187_out, not_188_out, not_189_out, F5, not_190_out, not_191_out, F2, not_192_out, not_193_out);
  and and_26 (and_26_out, not_194_out, not_195_out, not_196_out, not_197_out, not_198_out, not_199_out, F5, not_200_out, F3, not_201_out, F1, F0);
  and and_27 (and_27_out, not_202_out, not_203_out, OP3, not_204_out, not_205_out, not_206_out);
  and and_28 (and_28_out, not_207_out, not_208_out, OP3, OP2, not_209_out, not_210_out);
  and and_29 (and_29_out, not_211_out, not_212_out, OP3, not_213_out, not_214_out, OP0);
  and and_30 (and_30_out, OP5, not_215_out, not_216_out, not_217_out, OP1, OP0);
  and and_31 (and_31_out, OP5, not_218_out, OP3, not_219_out, OP1, OP0);
  and and_32 (and_32_out, OP5, not_220_out, not_221_out, not_222_out, not_223_out, not_224_out);
  and and_33 (and_33_out, not_225_out, not_226_out, not_227_out, not_228_out, not_229_out, not_230_out, F5, not_231_out, not_232_out, F2, not_233_out, F0);
  and and_34 (and_34_out, not_234_out, not_235_out, not_236_out, not_237_out, not_238_out, not_239_out, F5, not_240_out, not_241_out, F2, F1, F0);
  and and_35 (and_35_out, not_242_out, not_243_out, not_244_out, not_245_out, not_246_out, not_247_out, F5, not_248_out, F3, not_249_out, F1, not_250_out);
  and and_36 (and_36_out, not_251_out, not_252_out, not_253_out, not_254_out, not_255_out, not_256_out, F5, not_257_out, F3, not_258_out, F1, F0);
  and and_37 (and_37_out, not_259_out, not_260_out, OP3, not_261_out, OP1, not_262_out);
  and and_38 (and_38_out, not_263_out, not_264_out, OP3, OP2, not_265_out, OP0);
  and and_39 (and_39_out, not_266_out, not_267_out, not_268_out, not_269_out, not_270_out, not_271_out, F5, not_272_out, not_273_out, F2, F1, not_274_out);
  or or_1 (S1, and_14_out, and_15_out, and_16_out, and_17_out, and_18_out, and_19_out, and_20_out, and_21_out);
  or or_2 (S2, and_22_out, and_23_out, and_24_out, and_25_out, and_26_out, and_27_out, and_28_out, and_29_out, and_30_out, and_31_out, and_32_out);
  or or_3 (S3, and_33_out, and_34_out, and_35_out, and_36_out, and_37_out, and_38_out, and_39_out);
  or or_4 (S0, and_1_out, and_2_out, and_3_out, and_4_out, and_5_out, and_6_out, and_7_out, and_8_out, and_9_out, and_10_out, and_11_out, and_12_out, and_13_out);
endmodule

// 控制信号生成
module \控制信号自动生成  (
  input  OP0,
  input  OP1,
  input  OP2,
  input  OP3,
  input  OP4,
  input  OP5,
  input  F0,
  input  F1,
  input  F2,
  input  F3,
  input  F4,
  input  F5,
  output MemToReg,
  output MemWrite,
  output ALU_SRC,
  output RegWrite,
  output SysCALL,
  output SignedExt,
  output RegDst,
  output BEQ,
  output BNE,
  output JR,
  output JUMP,
  output JAL,
  output SRLV,
  output LB,
  output BGTZ,
  output mode1,
  output mode2
);

  wire and_1_out, and_2_out, and_4_out, and_5_out, and_6_out, and_7_out, and_8_out, and_9_out, and_10_out,
       and_11_out, and_12_out, and_13_out, and_14_out, and_15_out, and_16_out, and_17_out, and_19_out,
       and_20_out, and_21_out, and_22_out, and_23_out, and_24_out, and_25_out, and_26_out, and_27_out,
       and_28_out, and_32_out, and_33_out, not_1_out, not_2_out, not_3_out, not_4_out, not_5_out, not_6_out,
       not_7_out, not_8_out, not_9_out, not_10_out, not_11_out, not_12_out, not_13_out, not_14_out,
       not_15_out, not_16_out, not_17_out, not_18_out, not_19_out, not_20_out, not_21_out, not_22_out,
       not_23_out, not_24_out, not_25_out, not_26_out, not_27_out, not_28_out, not_29_out, not_30_out,
       not_31_out, not_32_out, not_33_out, not_34_out, not_35_out, not_36_out, not_37_out, not_38_out,
       not_39_out, not_40_out, not_41_out, not_42_out, not_43_out, not_44_out, not_45_out, not_46_out,
       not_47_out, not_48_out, not_49_out, not_50_out, not_51_out, not_52_out, not_53_out, not_54_out,
       not_55_out, not_56_out, not_57_out, not_58_out, not_59_out, not_60_out, not_61_out, not_62_out,
       not_63_out, not_64_out, not_65_out, not_66_out, not_67_out, not_68_out, not_69_out, not_70_out,
       not_71_out, not_72_out, not_73_out, not_74_out, not_75_out, not_76_out, not_77_out, not_78_out,
       not_79_out, not_80_out, not_81_out, not_82_out, not_83_out, not_84_out, not_85_out, not_86_out,
       not_87_out, not_88_out, not_89_out, not_90_out, not_91_out, not_92_out, not_93_out, not_94_out,
       not_95_out, not_96_out, not_97_out, not_98_out, not_99_out, not_100_out, not_101_out, not_102_out,
       not_103_out, not_104_out, not_105_out, not_106_out, not_107_out, not_108_out, not_109_out,
       not_110_out, not_111_out, not_112_out, not_113_out, not_114_out, not_115_out, not_116_out,
       not_117_out, not_118_out, not_119_out, not_120_out, not_121_out, not_122_out, not_123_out,
       not_124_out, not_125_out, not_126_out, not_127_out, not_128_out, not_129_out, not_130_out,
       not_131_out, not_132_out, not_133_out, not_134_out, not_135_out, not_136_out, not_137_out,
       not_138_out, not_139_out, not_140_out, not_141_out, not_142_out, not_143_out, not_144_out,
       not_145_out, not_146_out, not_147_out, not_148_out, not_149_out, not_150_out, not_151_out,
       not_152_out, not_153_out, not_154_out, not_155_out, not_156_out, not_157_out, not_158_out,
       not_159_out, not_160_out, not_161_out, not_162_out, not_163_out, not_164_out, not_165_out,
       not_166_out, not_167_out, not_168_out, not_169_out, not_170_out, not_171_out, not_172_out,
       not_173_out, not_174_out, not_175_out, not_176_out, not_177_out, not_178_out, not_179_out,
       not_180_out, not_181_out, not_182_out, not_183_out, not_184_out, not_185_out, not_186_out,
       not_187_out, not_188_out, not_189_out, not_190_out, not_191_out, not_192_out, not_193_out,
       not_194_out, not_195_out, not_196_out, not_197_out, not_198_out, not_199_out, not_200_out,
       not_201_out, not_202_out, not_203_out, not_204_out, not_205_out, not_206_out, not_207_out,
       not_208_out, not_209_out, not_210_out, not_211_out, not_212_out, not_213_out, not_214_out,
       not_215_out, not_216_out, not_217_out, not_218_out, not_219_out, not_220_out, not_221_out,
       not_222_out, not_223_out, not_224_out, not_225_out, not_226_out, not_227_out, not_228_out;

  not not_1 (not_1_out, OP0);
  not not_2 (not_2_out, OP1);
  not not_3 (not_3_out, OP2);
  not not_4 (not_4_out, OP3);
  not not_5 (not_5_out, OP4);
  not not_6 (not_6_out, OP2);
  not not_7 (not_7_out, OP3);
  not not_8 (not_8_out, OP4);
  not not_9 (not_9_out, OP2);
  not not_10 (not_10_out, OP4);
  not not_11 (not_11_out, OP0);
  not not_12 (not_12_out, OP1);
  not not_13 (not_13_out, OP2);
  not not_14 (not_14_out, OP3);
  not not_15 (not_15_out, OP4);
  not not_16 (not_16_out, OP0);
  not not_17 (not_17_out, OP2);
  not not_18 (not_18_out, OP4);
  not not_19 (not_19_out, OP5);
  not not_20 (not_20_out, OP1);
  not not_21 (not_21_out, OP4);
  not not_22 (not_22_out, OP5);
  not not_23 (not_23_out, OP2);
  not not_24 (not_24_out, OP4);
  not not_25 (not_25_out, OP0);
  not not_26 (not_26_out, OP1);
  not not_27 (not_27_out, OP2);
  not not_28 (not_28_out, OP3);
  not not_29 (not_29_out, OP4);
  not not_30 (not_30_out, F0);
  not not_31 (not_31_out, F2);
  not not_32 (not_32_out, F3);
  not not_33 (not_33_out, F4);
  not not_34 (not_34_out, OP0);
  not not_35 (not_35_out, OP1);
  not not_36 (not_36_out, OP2);
  not not_37 (not_37_out, OP3);
  not not_38 (not_38_out, OP4);
  not not_39 (not_39_out, F1);
  not not_40 (not_40_out, F3);
  not not_41 (not_41_out, F4);
  not not_42 (not_42_out, OP0);
  not not_43 (not_43_out, OP1);
  not not_44 (not_44_out, OP2);
  not not_45 (not_45_out, OP3);
  not not_46 (not_46_out, OP4);
  not not_47 (not_47_out, F3);
  not not_48 (not_48_out, F4);
  not not_49 (not_49_out, OP0);
  not not_50 (not_50_out, OP1);
  not not_51 (not_51_out, OP2);
  not not_52 (not_52_out, OP3);
  not not_53 (not_53_out, OP4);
  not not_54 (not_54_out, F0);
  not not_55 (not_55_out, F3);
  not not_56 (not_56_out, F4);
  not not_57 (not_57_out, OP0);
  not not_58 (not_58_out, OP1);
  not not_59 (not_59_out, OP2);
  not not_60 (not_60_out, OP3);
  not not_61 (not_61_out, OP4);
  not not_62 (not_62_out, F2);
  not not_63 (not_63_out, F3);
  not not_64 (not_64_out, F4);
  not not_65 (not_65_out, F5);
  not not_66 (not_66_out, OP0);
  not not_67 (not_67_out, OP1);
  not not_68 (not_68_out, OP2);
  not not_69 (not_69_out, OP3);
  not not_70 (not_70_out, OP4);
  not not_71 (not_71_out, F2);
  not not_72 (not_72_out, F4);
  not not_73 (not_73_out, OP0);
  not not_74 (not_74_out, OP1);
  not not_75 (not_75_out, OP2);
  not not_76 (not_76_out, OP3);
  not not_77 (not_77_out, OP4);
  not not_78 (not_78_out, OP0);
  not not_79 (not_79_out, OP2);
  not not_80 (not_80_out, OP4);
  not not_81 (not_81_out, OP5);
  not not_82 (not_82_out, OP1);
  not not_83 (not_83_out, OP4);
  not not_84 (not_84_out, OP5);
  not not_85 (not_85_out, OP2);
  not not_86 (not_86_out, OP3);
  not not_87 (not_87_out, OP4);
  not not_88 (not_88_out, OP0);
  not not_89 (not_89_out, OP1);
  not not_90 (not_90_out, OP2);
  not not_91 (not_91_out, OP3);
  not not_92 (not_92_out, OP4);
  not not_93 (not_93_out, OP5);
  not not_94 (not_94_out, F0);
  not not_95 (not_95_out, F1);
  not not_96 (not_96_out, F4);
  not not_97 (not_97_out, F5);
  not not_98 (not_98_out, OP0);
  not not_99 (not_99_out, OP1);
  not not_100 (not_100_out, OP2);
  not not_101 (not_101_out, OP3);
  not not_102 (not_102_out, OP4);
  not not_103 (not_103_out, OP0);
  not not_104 (not_104_out, OP2);
  not not_105 (not_105_out, OP4);
  not not_106 (not_106_out, OP5);
  not not_107 (not_107_out, OP1);
  not not_108 (not_108_out, OP2);
  not not_109 (not_109_out, OP4);
  not not_110 (not_110_out, OP5);
  not not_111 (not_111_out, OP2);
  not not_112 (not_112_out, OP4);
  not not_113 (not_113_out, OP0);
  not not_114 (not_114_out, OP1);
  not not_115 (not_115_out, OP2);
  not not_116 (not_116_out, OP3);
  not not_117 (not_117_out, OP4);
  not not_118 (not_118_out, OP5);
  not not_119 (not_119_out, F0);
  not not_120 (not_120_out, F1);
  not not_121 (not_121_out, F2);
  not not_122 (not_122_out, F4);
  not not_123 (not_123_out, F5);
  not not_124 (not_124_out, OP0);
  not not_125 (not_125_out, OP1);
  not not_126 (not_126_out, OP2);
  not not_127 (not_127_out, OP3);
  not not_128 (not_128_out, OP4);
  not not_129 (not_129_out, OP5);
  not not_130 (not_130_out, F1);
  not not_131 (not_131_out, F3);
  not not_132 (not_132_out, F4);
  not not_133 (not_133_out, OP0);
  not not_134 (not_134_out, OP1);
  not not_135 (not_135_out, OP2);
  not not_136 (not_136_out, OP3);
  not not_137 (not_137_out, OP4);
  not not_138 (not_138_out, OP5);
  not not_139 (not_139_out, F3);
  not not_140 (not_140_out, F4);
  not not_141 (not_141_out, OP0);
  not not_142 (not_142_out, OP1);
  not not_143 (not_143_out, OP2);
  not not_144 (not_144_out, OP3);
  not not_145 (not_145_out, OP4);
  not not_146 (not_146_out, OP5);
  not not_147 (not_147_out, F0);
  not not_148 (not_148_out, F3);
  not not_149 (not_149_out, F4);
  not not_150 (not_150_out, OP0);
  not not_151 (not_151_out, OP1);
  not not_152 (not_152_out, OP2);
  not not_153 (not_153_out, OP3);
  not not_154 (not_154_out, OP4);
  not not_155 (not_155_out, OP5);
  not not_156 (not_156_out, F2);
  not not_157 (not_157_out, F3);
  not not_158 (not_158_out, F4);
  not not_159 (not_159_out, F5);
  not not_160 (not_160_out, OP0);
  not not_161 (not_161_out, OP1);
  not not_162 (not_162_out, OP2);
  not not_163 (not_163_out, OP3);
  not not_164 (not_164_out, OP4);
  not not_165 (not_165_out, OP5);
  not not_166 (not_166_out, F2);
  not not_167 (not_167_out, F4);
  not not_168 (not_168_out, OP0);
  not not_169 (not_169_out, OP1);
  not not_170 (not_170_out, OP3);
  not not_171 (not_171_out, OP4);
  not not_172 (not_172_out, OP5);
  not not_173 (not_173_out, OP1);
  not not_174 (not_174_out, OP3);
  not not_175 (not_175_out, OP4);
  not not_176 (not_176_out, OP5);
  not not_177 (not_177_out, OP0);
  not not_178 (not_178_out, OP1);
  not not_179 (not_179_out, OP2);
  not not_180 (not_180_out, OP3);
  not not_181 (not_181_out, OP4);
  not not_182 (not_182_out, OP5);
  not not_183 (not_183_out, F0);
  not not_184 (not_184_out, F1);
  not not_185 (not_185_out, F2);
  not not_186 (not_186_out, F4);
  not not_187 (not_187_out, F5);
  not not_188 (not_188_out, OP0);
  not not_189 (not_189_out, OP2);
  not not_190 (not_190_out, OP3);
  not not_191 (not_191_out, OP4);
  not not_192 (not_192_out, OP5);
  not not_193 (not_193_out, F0);
  not not_194 (not_194_out, F1);
  not not_195 (not_195_out, F2);
  not not_196 (not_196_out, F4);
  not not_197 (not_197_out, F5);
  not not_198 (not_198_out, OP2);
  not not_199 (not_199_out, OP3);
  not not_200 (not_200_out, OP4);
  not not_201 (not_201_out, OP5);
  not not_202 (not_202_out, OP2);
  not not_203 (not_203_out, OP3);
  not not_204 (not_204_out, OP4);
  not not_205 (not_205_out, OP5);
  not not_206 (not_206_out, OP0);
  not not_207 (not_207_out, OP1);
  not not_208 (not_208_out, OP2);
  not not_209 (not_209_out, OP3);
  not not_210 (not_210_out, OP4);
  not not_211 (not_211_out, OP5);
  not not_212 (not_212_out, F0);
  not not_213 (not_213_out, F3);
  not not_214 (not_214_out, F4);
  not not_215 (not_215_out, F5);
  not not_216 (not_216_out, OP0);
  not not_217 (not_217_out, OP1);
  not not_218 (not_218_out, OP2);
  not not_219 (not_219_out, OP3);
  not not_220 (not_220_out, OP4);
  not not_221 (not_221_out, OP3);
  not not_222 (not_222_out, OP4);
  not not_223 (not_223_out, OP5);
  not not_224 (not_224_out, OP4);
  not not_225 (not_225_out, OP3);
  not not_226 (not_226_out, OP2);
  not not_227 (not_227_out, OP1);
  not not_228 (not_228_out, OP0);
  and and_1 (and_1_out, not_1_out, not_2_out, not_3_out, not_4_out, not_5_out, OP5);
  and and_2 (and_2_out, OP0, OP1, not_6_out, not_7_out, not_8_out, OP5);
  and and_3 (MemWrite, OP0, OP1, not_9_out, OP3, not_10_out, OP5);
  and and_4 (and_4_out, not_11_out, not_12_out, not_13_out, not_14_out, not_15_out, OP5);
  and and_5 (and_5_out, not_16_out, not_17_out, OP3, not_18_out, not_19_out);
  and and_6 (and_6_out, not_20_out, OP3, not_21_out, not_22_out);
  and and_7 (and_7_out, OP0, OP1, not_23_out, not_24_out, OP5);
  and and_8 (and_8_out, not_25_out, not_26_out, not_27_out, not_28_out, not_29_out, not_30_out, not_31_out, not_32_out, not_33_out);
  and and_9 (and_9_out, not_34_out, not_35_out, not_36_out, not_37_out, not_38_out, not_39_out, not_40_out, not_41_out, F5);
  and and_10 (and_10_out, not_42_out, not_43_out, not_44_out, not_45_out, not_46_out, F2, not_47_out, not_48_out, F5);
  and and_11 (and_11_out, not_49_out, not_50_out, not_51_out, not_52_out, not_53_out, not_54_out, F1, not_55_out, not_56_out);
  and and_12 (and_12_out, not_57_out, not_58_out, not_59_out, not_60_out, not_61_out, F1, not_62_out, not_63_out, not_64_out, not_65_out);
  and and_13 (and_13_out, not_66_out, not_67_out, not_68_out, not_69_out, not_70_out, F1, not_71_out, F3, not_72_out, F5);
  and and_14 (and_14_out, not_73_out, not_74_out, not_75_out, not_76_out, not_77_out, OP5);
  and and_15 (and_15_out, not_78_out, not_79_out, OP3, not_80_out, not_81_out);
  and and_16 (and_16_out, not_82_out, OP3, not_83_out, not_84_out);
  and and_17 (and_17_out, OP0, OP1, not_85_out, not_86_out, not_87_out);
  and and_18 (SysCALL, not_88_out, not_89_out, not_90_out, not_91_out, not_92_out, not_93_out, not_94_out, not_95_out, F2, F3, not_96_out, not_97_out);
  and and_19 (and_19_out, not_98_out, not_99_out, not_100_out, not_101_out, not_102_out, OP5);
  and and_20 (and_20_out, not_103_out, not_104_out, OP3, not_105_out, not_106_out);
  and and_21 (and_21_out, not_107_out, not_108_out, OP3, not_109_out, not_110_out);
  and and_22 (and_22_out, OP0, OP1, not_111_out, not_112_out, OP5);
  and and_23 (and_23_out, not_113_out, not_114_out, not_115_out, not_116_out, not_117_out, not_118_out, not_119_out, not_120_out, not_121_out, not_122_out, not_123_out);
  and and_24 (and_24_out, not_124_out, not_125_out, not_126_out, not_127_out, not_128_out, not_129_out, not_130_out, not_131_out, not_132_out, F5);
  and and_25 (and_25_out, not_133_out, not_134_out, not_135_out, not_136_out, not_137_out, not_138_out, F2, not_139_out, not_140_out, F5);
  and and_26 (and_26_out, not_141_out, not_142_out, not_143_out, not_144_out, not_145_out, not_146_out, not_147_out, F1, not_148_out, not_149_out);
  and and_27 (and_27_out, not_150_out, not_151_out, not_152_out, not_153_out, not_154_out, not_155_out, F1, not_156_out, not_157_out, not_158_out, not_159_out);
  and and_28 (and_28_out, not_160_out, not_161_out, not_162_out, not_163_out, not_164_out, not_165_out, F1, not_166_out, F3, not_167_out, F5);
  and and_29 (BEQ, not_168_out, not_169_out, OP2, not_170_out, not_171_out, not_172_out);
  and and_30 (BNE, OP0, not_173_out, OP2, not_174_out, not_175_out, not_176_out);
  and and_31 (JR, not_177_out, not_178_out, not_179_out, not_180_out, not_181_out, not_182_out, not_183_out, not_184_out, not_185_out, F3, not_186_out, not_187_out);
  and and_32 (and_32_out, not_188_out, not_189_out, not_190_out, not_191_out, not_192_out, not_193_out, not_194_out, not_195_out, F3, not_196_out, not_197_out);
  and and_33 (and_33_out, OP1, not_198_out, not_199_out, not_200_out, not_201_out);
  and and_34 (JAL, OP0, OP1, not_202_out, not_203_out, not_204_out, not_205_out);
  and and_35 (SRLV, not_206_out, not_207_out, not_208_out, not_209_out, not_210_out, not_211_out, not_212_out, F1, F2, not_213_out, not_214_out, not_215_out);
  and and_36 (LB, not_216_out, not_217_out, not_218_out, not_219_out, not_220_out, OP5);
  and and_37 (BGTZ, OP0, OP1, OP2, not_221_out, not_222_out, not_223_out);
  and and_38 (mode2, OP5, not_224_out, not_225_out, not_226_out, not_227_out, not_228_out);
  or or_1 (MemToReg, and_1_out, and_2_out);
  or or_2 (ALU_SRC, and_4_out, and_5_out, and_6_out, and_7_out);
  or or_3 (RegWrite, and_8_out, and_9_out, and_10_out, and_11_out, and_12_out, and_13_out, and_14_out, and_15_out, and_16_out, and_17_out);
  or or_4 (SignedExt, and_19_out, and_20_out, and_21_out, and_22_out);
  or or_5 (RegDst, and_23_out, and_24_out, and_25_out, and_26_out, and_27_out, and_28_out);
  or or_6 (JUMP, and_32_out, and_33_out);

  assign mode1 = 1'b0;
endmodule

// ALU
module MIPS_ALU (
  input  [4:0] shamt,
  input  [31:0] X,
  input  [31:0] Y,
  input  [3:0] AluOP,
  output Equal,
  output [31:0] Result,
  output [31:0] Result_2
);

  wire [0:0] comparator_1_lt, comparator_2_lt;
  wire [31:0] adder_1_out, AND_out, divider_1_out, divider_1_rem, multiplier_1_cout, multiplier_1_out,
       NOR_out, OR_out, shifter_1_out, shifter_2_out, shifter_3_out, subtractor_1_out, XOR_out;

  assign AND_out = X & Y;  // AND_Gate AND, 32 bits wide
  assign OR_out = X | Y;  // OR_Gate OR, 32 bits wide
  Shifter #(.width(32), .shift("ll")) shifter_1 (.in(Y), .\dist (shamt), .out(shifter_1_out));
  Shifter #(.width(32), .shift("ar")) shifter_2 (.in(Y), .\dist (shamt), .out(shifter_2_out));
  Shifter #(.width(32), .shift("lr")) shifter_3 (.in(Y), .\dist (shamt), .out(shifter_3_out));
  Multiplier #(.width(32)) multiplier_1 (.a(X), .b(Y), .out(multiplier_1_out), .cout(multiplier_1_cout));  // open: cin
  Divider #(.width(32)) divider_1 (.a(X), .b(Y), .out(divider_1_out), .rem(divider_1_rem));  // open: upper
  Adder #(.width(32)) adder_1 (.a(X), .b(Y), .out(adder_1_out));  // open: cin, cout
  Subtractor #(.width(32)) subtractor_1 (.a(X), .b(Y), .out(subtractor_1_out));  // open: bin, bout
  assign XOR_out = X ^ Y;  // XOR_Gate XOR, 32 bits wide
  assign NOR_out = ~(X | Y);  // NOR_Gate NOR, 32 bits wide
  Comparator #(.width(32), .mode("twosComplement")) comparator_1 (
    .a(X), .b(Y), .eq(Equal), .lt(comparator_1_lt[0]));  // open: gt
  Comparator #(.width(32), .mode("unsigned")) comparator_2 (.a(X), .b(Y), .lt(comparator_2_lt[0]));  // open: gt, eq
  Multiplexer #(.select(4), .width(32), .disabled("Z"), .enable("false")) multiplexer_1 (
    .in0(shifter_1_out), .in1(shifter_2_out), .in2(shifter_3_out), .in3(multiplier_1_out),
    .in4(divider_1_out), .in5(adder_1_out), .in6(subtractor_1_out), .in7(AND_out), .in8(OR_out),
    .in9(XOR_out), .in10(NOR_out), .in11({{31{1'b0}}, comparator_1_lt[0]}),
    .in12({{31{1'b0}}, comparator_2_lt[0]}), .in13({32{1'b0}}), .in14({32{1'b0}}), .in15({32{1'b0}}),
    .out(Result), .sel(AluOP));
  Multiplexer #(.select(4), .width(32), .disabled("Z"), .enable("false")) multiplexer_2 (
    .in0({32{1'b0}}), .in1({32{1'b0}}), .in2({32{1'b0}}), .in3(multiplier_1_cout), .in4(divider_1_rem),
    .in5({32{1'b0}}), .in6({32{1'b0}}), .in7({32{1'b0}}), .in8({32{1'b0}}), .in9({32{1'b0}}),
    .in10({32{1'b0}}), .in11({32{1'b0}}), .in12({32{1'b0}}), .in13({32{1'b0}}), .in14({32{1'b0}}),
    .in15({32{1'b0}}), .out(Result_2), .sel(AluOP));

  // Other names for the same wires on the sheet: Result2[31:0] = Result_2; S[3:0] = AluOP

  // Notes on the sheet:
  //   不要改变此引脚区域内容，也不要改变ALU封装形式
  //   输入引脚
  //   输出引脚
endmodule

module MIPS_Regifile (
  input  [31:0] Din,
  input  Clk,
  input  WE,
  input  [4:0] R1_num,
  input  [4:0] W_num,
  input  [4:0] R2_num,
  output [31:0] R1,
  output [31:0] R2
);

  // RegisterFile registerfile_1: pin names not known; wires that end beside it: Din, Clk, WE, W_num, R1_num, R2_num, R1, R2
endmodule
